// Logisim project 171044098.circ as structural Verilog: 10 circuits, main circuit main
module main (
  input  Random_Word,
  input  [7:0] a,
  input  [7:0] b,
  input  [7:0] c,
  input  [7:0] d,
  input  [7:0] e,
  input  [7:0] f,
  input  [7:0] g,
  input  [7:0] h
);

  wire a_out, b_out, c_out, clock_1_out, control_unit_1_game_over, control_unit_1_increment_led,
       control_unit_1_load_input, control_unit_1_load_number, control_unit_1_load_sum,
       control_unit_1_machine_win, control_unit_1_user_win, control_unit_1_write, control_unit_1_write_reset,
       d_out, datapath_1_fail, datapath_1_go, datapath_1_is_lost, datapath_1_is_win,
       datapath_1_writing_all_is_done, datapath_1_writing_is_done, e_out, f_out, g_out, getchoose_1_is_input,
       h_out, i_out, j_out, k_out, l_out, m_out, n_out, o_out, p_out, q_out, r_out, Reset_Score_out, s_out,
       Start_Game_out, t_out, u_out, v_out, w_out, x_out, y_out, z_out;
  wire [3:0] datapath_1_led_number, datapath_1_m_1, datapath_1_m_2, datapath_1_m_3, datapath_1_number,
       datapath_1_u_1, datapath_1_u_2, datapath_1_u_3;
  wire [7:0] datapath_1_current_letter, getchoose_1_input;
  wire [8:4] datapath_1_number_2;
  wire [14:0] hanging_man_1__0, hanging_man_1__1, hanging_man_1__2, hanging_man_1__3, hanging_man_1__4,
       hanging_man_1__5, hanging_man_1__6, hanging_man_1__7, hanging_man_1__8, hanging_man_1__9;

  DotMatrix #(.matrixcols(10), .matrixrows(15)) dotmatrix_1 (
    .col0(hanging_man_1__0), .col1(hanging_man_1__1), .col2(hanging_man_1__2), .col3(hanging_man_1__3),
    .col4(hanging_man_1__4), .col5(hanging_man_1__5), .col6(hanging_man_1__6), .col7(hanging_man_1__7),
    .col8(hanging_man_1__8), .col9(hanging_man_1__9));
  hanging_man hanging_man_1 (
    .led_number(datapath_1_led_number), ._0(hanging_man_1__0), ._1(hanging_man_1__1), ._2(hanging_man_1__2),
    ._3(hanging_man_1__3), ._4(hanging_man_1__4), ._5(hanging_man_1__5), ._6(hanging_man_1__6),
    ._7(hanging_man_1__7), ._8(hanging_man_1__8), ._9(hanging_man_1__9));
  Button u_a (.out(a_out));
  Button Start_Game (.out(Start_Game_out));
  Button u_b (.out(b_out));
  Button u_c (.out(c_out));
  Hex_Digit_Display hex_digit_display_1 (.value(datapath_1_number));  // open: dp
  Button u_d (.out(d_out));
  Button u_e (.out(e_out));
  Datapath datapath_1 (
    .a(a), .\input (getchoose_1_input), .b(b), .load_input(getchoose_1_is_input), .c(c), .d(d), .e(e), .f(f),
    .g(g), .h(h), .plus_1_led_Number(control_unit_1_increment_led), .get_next_word(Start_Game_out),
    .select_word_type(Random_Word), .clk(clock_1_out), .user_win(control_unit_1_user_win),
    .reset_score(Reset_Score_out), .machine_win(control_unit_1_machine_win), .write(control_unit_1_write),
    .led_number(datapath_1_led_number), .u_2(datapath_1_u_2), .u_3(datapath_1_u_3), .m_2(datapath_1_m_2),
    .m_3(datapath_1_m_3), .u_1(datapath_1_u_1), .m_1(datapath_1_m_1),
    .current_letter(datapath_1_current_letter), .load_number(control_unit_1_load_number),
    .number({datapath_1_number_2, datapath_1_number}), .is_win(datapath_1_is_win),
    .game_over(control_unit_1_game_over), .load_sum(control_unit_1_load_sum), .is_lost(datapath_1_is_lost),
    .reset_write(control_unit_1_write_reset), .writing_is_done(datapath_1_writing_is_done),
    .writing_all_is_done(datapath_1_writing_all_is_done), .reset_write_all_word(control_unit_1_load_number),
    .fail(datapath_1_fail), .go(datapath_1_go), .reset_go(control_unit_1_write_reset),
    .start_go(control_unit_1_load_input));
  Button u_g (.out(g_out));
  Button u_f (.out(f_out));
  Button i (.out(i_out));
  Button u_h (.out(h_out));
  getChoose getchoose_1 (
    .a(a_out), .b(b_out), .c(c_out), .d(d_out), .e(e_out), .f(f_out), .g(g_out), .h(h_out), .i(i_out),
    .j(j_out), .k(k_out), .l(l_out), .m(m_out), .n(n_out), .o(o_out), .p(p_out), .q(q_out), .r(r_out),
    .s(s_out), .t(t_out), .u(u_out), .v(v_out), .w(w_out), .x(x_out), .y(y_out), .z(z_out),
    .\input (getchoose_1_input), .is_input(getchoose_1_is_input));
  Button j (.out(j_out));
  Button k (.out(k_out));
  Button l (.out(l_out));
  Button m (.out(m_out));
  control_unit control_unit_1 (
    .start(Start_Game_out), .is_win(datapath_1_is_win), .is_lost(datapath_1_is_lost), .fail(datapath_1_fail),
    .\input (getchoose_1_is_input), .writing_is_done(datapath_1_writing_is_done),
    .writing_all_is_done(datapath_1_writing_all_is_done), .clk(clock_1_out), .write(control_unit_1_write),
    .write_reset(control_unit_1_write_reset), .machine_win(control_unit_1_machine_win),
    .game_over(control_unit_1_game_over), .load_number(control_unit_1_load_number),
    .increment_led(control_unit_1_increment_led), .load_sum(control_unit_1_load_sum),
    .user_win(control_unit_1_user_win), .go(datapath_1_go), .load_input(control_unit_1_load_input));
  Button o (.out(o_out));
  Button n (.out(n_out));
  Button p (.out(p_out));
  Button q (.out(q_out));
  Hex_Digit_Display hex_digit_display_2 (.value(datapath_1_u_3));  // open: dp
  Button Reset_Score (.out(Reset_Score_out));
  Button r (.out(r_out));
  Button s (.out(s_out));
  TTY tty_1 (.data(datapath_1_current_letter[6:0]), .clk(clock_1_out), .we(control_unit_1_write), .clr(Start_Game_out));
  Hex_Digit_Display hex_digit_display_3 (.value(datapath_1_u_1));  // open: dp
  Hex_Digit_Display hex_digit_display_4 (.value(datapath_1_u_2));  // open: dp
  Button u (.out(u_out));
  Button t (.out(t_out));
  Hex_Digit_Display hex_digit_display_5 (.value(datapath_1_m_3));  // open: dp
  Button v (.out(v_out));
  Button w (.out(w_out));
  Hex_Digit_Display hex_digit_display_6 (.value(datapath_1_m_2));  // open: dp
  Button x (.out(x_out));
  Button y (.out(y_out));
  Hex_Digit_Display hex_digit_display_7 (.value(datapath_1_m_1));  // open: dp
  Button z (.out(z_out));
  Clock clock_1 (.out(clock_1_out));

  // Notes on the sheet:
  //   Hanging Man
  //   number_of_chrcter
  //   User Score
  //   Word
  //   Machine Score
endmodule

module Datapath (
  input  [7:0] a,
  input  load_number,
  input  [7:0] \input ,
  input  [7:0] b,
  input  game_over,
  input  load_input,
  input  [7:0] c,
  input  [7:0] d,
  input  [7:0] e,
  input  [7:0] f,
  input  load_sum,
  input  [7:0] g,
  input  reset_go,
  input  [7:0] h,
  input  start_go,
  input  get_next_word,
  input  plus_1_led_Number,
  input  select_word_type,
  input  clk,
  input  user_win,
  input  reset_score,
  input  machine_win,
  input  reset_write,
  input  reset_write_all_word,
  input  write,
  output [8:0] number,
  output fail,
  output go,
  output is_win,
  output [3:0] led_number,
  output [3:0] u_2,
  output [3:0] u_3,
  output [3:0] m_2,
  output [3:0] m_3,
  output [3:0] u_1,
  output is_lost,
  output [3:0] m_1,
  output [7:0] current_letter,
  output writing_all_is_done,
  output writing_is_done
);

  wire check_word_1_a_ok, check_word_1_b_ok, check_word_1_c_ok, check_word_1_d_ok, check_word_1_e_ok,
       check_word_1_f_ok, check_word_1_g_ok, check_word_1_h_ok, comparator_1_gt, comparator_1_lt,
       comparator_2_eq, counter_3_carry, counter_4_carry, counter_7_carry, counter_8_carry, is_in_1_a_out,
       is_in_1_b_out, is_in_1_c_out, is_in_1_d_out, is_in_1_e_out, is_in_1_f_out, is_in_1_g_out,
       is_in_1_h_out, is_win_1_a_res, is_win_1_b_res, is_win_1_c_res, is_win_1_d_res, is_win_1_e_res,
       is_win_1_f_res, is_win_1_g_res, is_win_1_h_res, not_1_out, or_1_out, or_2_out, or_3_out, or_4_out,
       or_5_out;
  wire [7:0] get_word_a_out, get_word_b_out, get_word_c_out, get_word_d_out, get_word_e_out, get_word_f_out,
       get_word_g_out, get_word_h_out, register_2_q;
  wire [8:0] check_word_1_number, is_win_1_sum, register_3_q;

  select_word get_word (
    .a(a), .b(b), .c(c), .count(get_next_word), .d(d), .e(e), .f(f), .g(g), .h(h), .select(select_word_type),
    .a_out(get_word_a_out), .b_out(get_word_b_out), .c_out(get_word_c_out), .d_out(get_word_d_out),
    .e_out(get_word_e_out), .f_out(get_word_f_out), .g_out(get_word_g_out), .h_out(get_word_h_out));
  check_word check_word_1 (
    .a(get_word_a_out), .e(get_word_e_out), .b(get_word_b_out), .f(get_word_f_out), .c(get_word_c_out),
    .g(get_word_g_out), .d(get_word_d_out), .h(get_word_h_out), .number(check_word_1_number),
    .a_ok(check_word_1_a_ok), .b_ok(check_word_1_b_ok), .c_ok(check_word_1_c_ok), .d_ok(check_word_1_d_ok),
    .e_ok(check_word_1_e_ok), .f_ok(check_word_1_f_ok), .g_ok(check_word_1_g_ok), .h_ok(check_word_1_h_ok));
  write_word write_word_1 (
    .a(get_word_a_out), .b(get_word_b_out), .write(write), .a_ok(check_word_1_a_ok),
    .b_ok(check_word_1_b_ok), .c(get_word_c_out), .c_ok(check_word_1_c_ok), .d(get_word_d_out),
    .d_ok(check_word_1_d_ok), .e(get_word_e_out), .e_ok(check_word_1_e_ok), .f(get_word_f_out),
    .f_ok(check_word_1_f_ok), .g_ok(check_word_1_g_ok), .g(get_word_g_out), .h_ok(check_word_1_h_ok),
    .h(get_word_h_out), .found_h(is_win_1_h_res), .clk(clk), .current_letter(current_letter),
    .found_a(is_win_1_a_res), .found_b(is_win_1_b_res), .found_c(is_win_1_c_res), .found_d(is_win_1_d_res),
    .found_e(is_win_1_e_res), .found_f(is_win_1_f_res), .found_g(is_win_1_g_res), .reset_write(reset_write),
    .reset_write_all_word(reset_write_all_word), .write_all_word(game_over),
    .writing_is_done(writing_is_done), .writing_all_is_done(writing_all_is_done));
  Register #(.width(9)) register_1 (.D(check_word_1_number), .en(load_number), .Q(number), .clk(clk), .clr(game_over));
  Counter #(.width(4), .max('ha), .ongoal("stay")) counter_1 (
    .count(1'b1), .Q(led_number), .clk(plus_1_led_Number), .clr(writing_all_is_done));  // open: load, D, carry
  Register register_2 (.D(\input ), .en(load_input), .Q(register_2_q), .clk(clk), .clr(game_over));
  Comparator #(.width(4), .mode("unsigned")) comparator_1 (
    .a(led_number), .b(4'b1010), .gt(comparator_1_gt), .eq(is_lost), .lt(comparator_1_lt));
  is_in is_in_1 (
    .\input (register_2_q), .e(get_word_e_out), .a(get_word_a_out), .f(get_word_f_out), .b(get_word_b_out),
    .g(get_word_g_out), .c(get_word_c_out), .h(get_word_h_out), .d(get_word_d_out), .e_out(is_in_1_e_out),
    .a_out(is_in_1_a_out), .f_out(is_in_1_f_out), .b_out(is_in_1_b_out), .g_out(is_in_1_g_out),
    .c_out(is_in_1_c_out), .h_out(is_in_1_h_out), .d_out(is_in_1_d_out));
  // Probe on get_word_a_out
  // Probe on get_word_b_out
  // Probe on get_word_c_out
  // Probe on get_word_d_out
  // Probe on get_word_e_out
  // Probe on get_word_f_out
  // Probe on get_word_g_out
  // Probe on get_word_h_out
  is_win is_win_1 (
    .a_ok(check_word_1_a_ok), .is_in_a(is_in_1_a_out), .b_ok(check_word_1_b_ok), .is_in_b(is_in_1_b_out),
    .c_ok(check_word_1_c_ok), .is_in_c(is_in_1_c_out), .d_ok(check_word_1_d_ok), .is_in_d(is_in_1_d_out),
    .e_ok(check_word_1_e_ok), .is_in_e(is_in_1_e_out), .f_ok(check_word_1_f_ok), .is_in_f(is_in_1_f_out),
    .g_ok(check_word_1_g_ok), .is_in_g(is_in_1_g_out), .h_ok(check_word_1_h_ok), .number(number),
    .is_in_h(is_in_1_h_out), .clk(clk), .game_over(game_over), .is_win(is_win), .a_res(is_win_1_a_res),
    .b_res(is_win_1_b_res), .c_res(is_win_1_c_res), .d_res(is_win_1_d_res), .e_res(is_win_1_e_res),
    .f_res(is_win_1_f_res), .g_res(is_win_1_g_res), .h_res(is_win_1_h_res), .sum(is_win_1_sum));
  Counter #(.width(4), .max('h9)) counter_2 (
    .Q(u_3), .clk(counter_3_carry), .clr(reset_score));  // open: load, D, count, carry
  Counter #(.width(4), .max('ha)) counter_3 (
    .Q(u_2), .carry(counter_3_carry), .clk(counter_4_carry), .clr(or_2_out));  // open: load, D, count
  Counter #(.width(4), .max('ha)) counter_4 (
    .Q(u_1), .carry(counter_4_carry), .clk(user_win), .clr(or_1_out));  // open: load, D, count
  or or_1 (or_1_out, counter_4_carry, reset_score);
  or or_2 (or_2_out, counter_3_carry, reset_score);
  not not_1 (not_1_out, or_3_out);
  or or_3 (or_3_out, is_in_1_a_out, is_in_1_b_out, is_in_1_c_out, is_in_1_d_out, is_in_1_e_out, is_in_1_f_out, is_in_1_h_out, is_in_1_g_out);
  Register #(.width(9)) register_3 (.D(is_win_1_sum), .en(load_sum), .Q(register_3_q), .clk(clk), .clr(game_over));
  Counter #(.width(4), .max('h9)) counter_5 (
    .Q(m_3), .clk(counter_7_carry), .clr(reset_score));  // open: load, D, count, carry
  Comparator #(.width(9), .mode("unsigned")) comparator_2 (
    .a(is_win_1_sum), .b(register_3_q), .eq(comparator_2_eq));  // open: gt, lt
  Counter #(.width(3), .max('h7), .ongoal("stay")) counter_6 (
    .count(start_go), .carry(go), .clk(clk), .clr(reset_go));  // open: load, D, Q
  Counter #(.width(4), .max('ha)) counter_7 (
    .Q(m_2), .carry(counter_7_carry), .clk(counter_8_carry), .clr(or_5_out));  // open: load, D, count
  and and_1 (fail, not_1_out, comparator_2_eq);
  Counter #(.width(4), .max('ha)) counter_8 (
    .Q(m_1), .carry(counter_8_carry), .clk(machine_win), .clr(or_4_out));  // open: load, D, count
  or or_4 (or_4_out, reset_score, counter_8_carry);
  or or_5 (or_5_out, reset_score, counter_7_carry);

  // Notes on the sheet:
  //   write_word_tty
  //   is_win
endmodule

// get_number
module check_word (
  input  [7:0] a,
  input  [7:0] e,
  input  [7:0] b,
  input  [7:0] f,
  input  [7:0] c,
  input  [7:0] g,
  input  [7:0] d,
  input  [7:0] h,
  output a_ok,
  output e_ok,
  output b_ok,
  output f_ok,
  output c_ok,
  output g_ok,
  output d_ok,
  output [8:0] number,
  output h_ok
);

  wire adder_1_cout, adder_2_cout, adder_3_cout, adder_4_cout, adder_5_cout, adder_6_cout, comparator_1_lt,
       comparator_2_gt, comparator_3_lt, comparator_4_gt, comparator_5_lt, comparator_6_gt, comparator_7_lt,
       comparator_8_gt, comparator_9_gt, comparator_10_lt, comparator_11_gt, comparator_12_lt,
       comparator_13_gt, comparator_14_lt, comparator_15_gt, comparator_16_lt;
  wire [8:0] adder_1_out, adder_2_out, adder_3_out, adder_4_out, adder_5_out, adder_6_out,
       bit_extender_1_out, bit_extender_2_out, bit_extender_3_out, bit_extender_4_out, bit_extender_5_out,
       bit_extender_6_out, bit_extender_7_out, bit_extender_8_out;

  Comparator comparator_1 (.a(d), .b(8'h7b), .lt(comparator_1_lt));  // open: gt, eq
  Comparator comparator_2 (.a(a), .b(8'h60), .gt(comparator_2_gt));  // open: eq, lt
  Comparator comparator_3 (.a(a), .b(8'h7b), .lt(comparator_3_lt));  // open: gt, eq
  Comparator comparator_4 (.a(b), .b(8'h60), .gt(comparator_4_gt));  // open: eq, lt
  Comparator comparator_5 (.a(b), .b(8'h7b), .lt(comparator_5_lt));  // open: gt, eq
  Comparator comparator_6 (.a(c), .b(8'h60), .gt(comparator_6_gt));  // open: eq, lt
  Comparator comparator_7 (.a(c), .b(8'h7b), .lt(comparator_7_lt));  // open: gt, eq
  Comparator comparator_8 (.a(d), .b(8'h60), .gt(comparator_8_gt));  // open: eq, lt
  and and_1 (a_ok, comparator_2_gt, comparator_3_lt);
  and and_2 (b_ok, comparator_4_gt, comparator_5_lt);
  and and_3 (c_ok, comparator_6_gt, comparator_7_lt);
  and and_4 (d_ok, comparator_8_gt, comparator_1_lt);
  assign bit_extender_1_out = {{8{1'b0}}, a_ok};  // Bit_Extender bit_extender_1
  assign bit_extender_2_out = {{8{1'b0}}, b_ok};  // Bit_Extender bit_extender_2
  assign bit_extender_3_out = {{8{1'b0}}, c_ok};  // Bit_Extender bit_extender_3
  assign bit_extender_4_out = {{8{1'b0}}, d_ok};  // Bit_Extender bit_extender_4
  Adder #(.width(9)) adder_1 (
    .a(bit_extender_1_out), .b(bit_extender_2_out), .out(adder_1_out), .cout(adder_1_cout));  // open: cin
  Adder #(.width(9)) adder_2 (
    .a(adder_1_out), .b(bit_extender_3_out), .out(adder_2_out), .cin(adder_1_cout), .cout(adder_2_cout));
  Adder #(.width(9)) adder_3 (
    .a(adder_2_out), .b(bit_extender_4_out), .out(adder_3_out), .cin(adder_2_cout), .cout(adder_3_cout));
  Comparator comparator_9 (.a(e), .b(8'h60), .gt(comparator_9_gt));  // open: eq, lt
  Comparator comparator_10 (.a(e), .b(8'h7b), .lt(comparator_10_lt));  // open: gt, eq
  Comparator comparator_11 (.a(f), .b(8'h60), .gt(comparator_11_gt));  // open: eq, lt
  Comparator comparator_12 (.a(f), .b(8'h7b), .lt(comparator_12_lt));  // open: gt, eq
  Comparator comparator_13 (.a(g), .b(8'h60), .gt(comparator_13_gt));  // open: eq, lt
  Comparator comparator_14 (.a(g), .b(8'h7b), .lt(comparator_14_lt));  // open: gt, eq
  Comparator comparator_15 (.a(h), .b(8'h60), .gt(comparator_15_gt));  // open: eq, lt
  Comparator comparator_16 (.a(h), .b(8'h7b), .lt(comparator_16_lt));  // open: gt, eq
  and and_5 (e_ok, comparator_9_gt, comparator_10_lt);
  and and_6 (f_ok, comparator_11_gt, comparator_12_lt);
  and and_7 (g_ok, comparator_13_gt, comparator_14_lt);
  and and_8 (h_ok, comparator_15_gt, comparator_16_lt);
  assign bit_extender_5_out = {{8{1'b0}}, e_ok};  // Bit_Extender bit_extender_5
  assign bit_extender_6_out = {{8{1'b0}}, f_ok};  // Bit_Extender bit_extender_6
  assign bit_extender_7_out = {{8{1'b0}}, g_ok};  // Bit_Extender bit_extender_7
  assign bit_extender_8_out = {{8{1'b0}}, h_ok};  // Bit_Extender bit_extender_8
  Adder #(.width(9)) adder_4 (
    .a(adder_3_out), .b(bit_extender_5_out), .out(adder_4_out), .cin(adder_3_cout), .cout(adder_4_cout));
  Adder #(.width(9)) adder_5 (
    .a(adder_4_out), .b(bit_extender_6_out), .out(adder_5_out), .cin(adder_4_cout), .cout(adder_5_cout));
  Adder #(.width(9)) adder_6 (
    .a(adder_5_out), .b(bit_extender_7_out), .out(adder_6_out), .cin(adder_5_cout), .cout(adder_6_cout));
  Adder #(.width(9)) adder_7 (.a(adder_6_out), .b(bit_extender_8_out), .out(number), .cin(adder_6_cout));  // open: cout
endmodule

module is_in (
  input  [7:0] \input ,
  input  [7:0] e,
  input  [7:0] a,
  input  [7:0] f,
  input  [7:0] b,
  input  [7:0] g,
  input  [7:0] c,
  input  [7:0] h,
  input  [7:0] d,
  output e_out,
  output a_out,
  output f_out,
  output b_out,
  output g_out,
  output c_out,
  output h_out,
  output d_out
);

  Comparator comparator_1 (.a(a), .b(\input ), .eq(a_out));  // open: gt, lt
  Comparator comparator_2 (.a(b), .b(\input ), .eq(b_out));  // open: gt, lt
  Comparator comparator_3 (.a(c), .b(\input ), .eq(c_out));  // open: gt, lt
  Comparator comparator_4 (.a(d), .b(\input ), .eq(d_out));  // open: gt, lt
  Comparator comparator_5 (.a(g), .b(\input ), .eq(g_out));  // open: gt, lt
  Comparator comparator_6 (.a(h), .b(\input ), .eq(h_out));  // open: gt, lt
  Comparator comparator_7 (.a(e), .b(\input ), .eq(e_out));  // open: gt, lt
  Comparator comparator_8 (.a(f), .b(\input ), .eq(f_out));  // open: gt, lt
endmodule

module select_word (
  input  [7:0] a,
  input  [7:0] b,
  input  [7:0] c,
  input  count,
  input  [7:0] d,
  input  [7:0] e,
  input  [7:0] f,
  input  [7:0] g,
  input  [7:0] h,
  input  select,
  output [7:0] a_out,
  output [7:0] b_out,
  output [7:0] c_out,
  output [7:0] d_out,
  output [7:0] e_out,
  output [7:0] f_out,
  output [7:0] g_out,
  output [7:0] h_out
);

  wire [6:0] random_1_out;
  wire [7:0] bitselector_1_out, bitselector_2_out, bitselector_3_out, bitselector_4_out, bitselector_5_out,
       bitselector_6_out, bitselector_7_out, bitselector_8_out;
  wire [31:0] rom_1_data, rom_2_data;

  Random #(.width(7)) random_1 (.clk(count), .next(1'b1), .out(random_1_out));  // open: clr
  ROM #(.addrWidth(7), .dataWidth(32)) rom_1 (.addr(random_1_out), .data(rom_1_data), .sel(1'b1));
  ROM #(.addrWidth(7), .dataWidth(32)) rom_2 (.addr(random_1_out), .data(rom_2_data), .sel(1'b1));
  BitSelector #(.width(32), .group(8)) bitselector_1 (.in(rom_1_data), .out(bitselector_1_out), .sel(2'b11));
  BitSelector #(.width(32), .group(8)) bitselector_2 (.in(rom_1_data), .out(bitselector_2_out), .sel(2'b10));
  BitSelector #(.width(32), .group(8)) bitselector_3 (.in(rom_1_data), .out(bitselector_3_out), .sel(2'b01));
  BitSelector #(.width(32), .group(8)) bitselector_4 (.in(rom_1_data), .out(bitselector_4_out), .sel(2'b00));
  BitSelector #(.width(32), .group(8)) bitselector_5 (.in(rom_2_data), .out(bitselector_5_out), .sel(2'b11));
  BitSelector #(.width(32), .group(8)) bitselector_6 (.in(rom_2_data), .out(bitselector_6_out), .sel(2'b10));
  BitSelector #(.width(32), .group(8)) bitselector_7 (.in(rom_2_data), .out(bitselector_7_out), .sel(2'b01));
  BitSelector #(.width(32), .group(8)) bitselector_8 (.in(rom_2_data), .out(bitselector_8_out), .sel(2'b00));
  Multiplexer #(.width(8), .enable("false")) multiplexer_1 (
    .in0(a), .in1(bitselector_1_out), .out(a_out), .sel(select));
  Multiplexer #(.width(8), .enable("false")) multiplexer_2 (
    .in0(b), .in1(bitselector_2_out), .out(b_out), .sel(select));
  Multiplexer #(.width(8), .enable("false")) multiplexer_3 (
    .in0(c), .in1(bitselector_3_out), .out(c_out), .sel(select));
  Multiplexer #(.width(8), .enable("false")) multiplexer_4 (
    .in0(d), .in1(bitselector_4_out), .out(d_out), .sel(select));
  Multiplexer #(.width(8), .enable("false")) multiplexer_5 (
    .in0(e), .in1(bitselector_5_out), .out(e_out), .sel(select));
  Multiplexer #(.width(8), .enable("false")) multiplexer_6 (
    .in0(f), .in1(bitselector_6_out), .out(f_out), .sel(select));
  Multiplexer #(.width(8), .enable("false")) multiplexer_7 (
    .in0(g), .in1(bitselector_7_out), .out(g_out), .sel(select));
  Multiplexer #(.width(8), .enable("false")) multiplexer_8 (
    .in0(h), .in1(bitselector_8_out), .out(h_out), .sel(select));

  // Notes on the sheet:
  //   Random number Generator
  //   First 4 letter
  //   Last 4 Letter
  //   contents of rom_1 (hex, n*v repeats v):
  //   666f7867 0 6963 676f 726571 6a 6b69 77 0 77616c 63 626f 6e6f7761 65 7570 77686f6d 6176 63726f 0
  //   6672697a 63 6d6172 7265 64 73 6a756b 626f 747765 7769 6a 6b 676c6f77 667563 6d6e656d 6879 7a 677261
  //   62757a 6b696c6f 717569 66 66 6a6f 44 627566 61 756e6b 647761 73747265 696e 7768 64697a7a 62 6761
  //   64616971 62 6a6f 75 6a 7061 0 72 77 71 6461 706f7373 6769 6c 6c656e 676e6f 71 62757a 6475 6672617a
  //   61776b 0 676e 6a6f 6a69 7a69 6d61 6f78 67 6b6e6170 626c697a 7363686e 6e6170 6a6f67 0 61 79 627566
  //   7768697a 70 6661 7175 0 72 7268 6469 776869 6275636b 68 6669 61 6761 626f6f6b 0 7a69 656d6265 637573
  //   6465 7477656c 736372 646973 70 70757a7a 636f6f 6a 756e776f 626f 71756978 796f7574 6f7869 737472 69
  //   7275 67
  //   contents of rom_2 (hex, n*v repeats v):
  //   6c6f7665 77617665 65626f78 73736970 75697265 617a7a79 74736368 696d7079 6a696e78 6b776179 79636c65
  //   7866756c 64617973 71756970 746f776e 65766572 656e7565 71756574 77617679 7a6c6564 72797074 71756973
  //   63616c6c 65707468 74616666 65626f78 78636172 6c667468 7a617264 75696379 6c75747a 776f726d 68736961
  //   6f6e6963 7068656e 696c6368 62626564 7a696e67 62797465 7a7a6573 756e6e79 6f6c6b73 636b6579 616e6e79
  //   66616c6f 7a757265 6e6f776e 72766573 6e677468 6a757279 65657a79 79696e67 6c69747a 7a65626f 75697269
  //   75786f6d 7966756c 6e7a6970 756d626f 6a616d61 72757368 68796d65 616c747a 75697073 6d616765 69626c79
  //   616f7572 75636b79 67746873 73746963 75657565 7a617264 706c6578 7a6c6564 77617264 66696c6d 61726c79
  //   6b696e67 67736177 70706572 74726978 7967656e 6c797068 7361636b 7a617264 61707073 68746861 67696e67
  //   666f7274 736b6577 756d6d79 666f6f6e 7a696e67 72696465 63696e67 6172747a 73616c65 6f636b79 7974686d
  //   726e646c 736b6579 61726f6f 61696b75 6e657374 78696f6d 72616765 776f726d 77617879 677a6167 7a7a6c65
  //   746f6d73 65706c79 66746873 61746368 61766f77 6978656c 6c696e67 6b696573 656c6c79 72746879 67676c65
  //   6f746963 6866756c 64697a65 65746368 766f7279 62626564 697a6d6f
  //   0 - foxglove 1 - wave 2 - icebox 3 - gossip 4 - require 5 - jazzy 6 - kitsch 7 - wimpy 8 - jinx 9 - walkway a - cycle b - boxful c - nowadays d - equip e - uptown f - whomever 10 - avenue 11 - croquet 12 - wavy 13 - frizzled 14 - crypt 15 - marquis 16 - recall 17 - depth 18 - staff 19 - jukebox 1a - boxcar 1b - twelfth 1c - wizard 1d - juicy 1e - klutz 1f - glowworm 20 - fuchsia 21 - mnemonic 22 - hyphen 23 - zilch 24 - grabbed 25 - buzzing 26 - kilobyte 27 - quizzes 28 - funny 29 - folks 2a - jockey 2b - Danny 2c - buffalo 2d - azure 2e - unknown 2f - dwarves 30 - strength 31 - injury 32 - wheezy 33 - dizzying 34 - blitz 35 - gazebo 36 - daiquiri 37 - buxom 38 - joyful 39 - unzip 3a - jumbo 3b - pajama 3c - rush 3d - rhyme 3e - waltz 3f - quips 40 - damage 41 - possibly 42 - giaour 43 - lucky 44 - lengths 45 - gnostic 46 - queue 47 - buzzard 48 - duplex 49 - frazzled 4a - awkward 4b - film 4c - gnarly 4d - joking 4e - jigsaw 4f - zipper 50 - matrix 51 - oxygen 52 - glyph 53 - knapsack 54 - blizzard 55 - schnapps 56 - naphtha 57 - jogging 58 - fort 59 - askew 5a - yummy 5b - buffoon 5c - whizzing 5d - pride 5e - facing 5f - quartz 60 - sale 61 - rocky 62 - rhythm 63 - dirndl 64 - whiskey 65 - buckaroo 66 - haiku 67 - finest 68 - axiom 69 - garage 6a - bookworm 6b - waxy 6c - zigzag 6d - embezzle 6e - customs 6f - deeply 70 - twelfths 71 - scratch 72 - disavow 73 - pixel 74 - puzzling 75 - cookies 76 - jelly 77 - unworthy 78 - boggle 79 - quixotic 7a - youthful 7b - oxidize 7c - stretch 7d - ivory 7e - rubbed 7f - gizmo
endmodule

module write_word (
  input  [7:0] a,
  input  found_a,
  input  [7:0] b,
  input  write,
  input  a_ok,
  input  found_b,
  input  b_ok,
  input  [7:0] c,
  input  found_c,
  input  c_ok,
  input  [7:0] d,
  input  d_ok,
  input  found_d,
  input  [7:0] e,
  input  e_ok,
  input  found_e,
  input  [7:0] f,
  input  f_ok,
  input  found_f,
  input  g_ok,
  input  [7:0] g,
  input  reset_write,
  input  h_ok,
  input  found_g,
  input  [7:0] h,
  input  found_h,
  input  clk,
  input  write_all_word,
  input  reset_write_all_word,
  output writing_is_done,
  output [7:0] current_letter,
  output writing_all_is_done
);

  wire and_1_out, and_2_out, and_3_out, and_4_out, and_5_out, and_6_out, and_7_out, and_8_out, not_1_out,
       not_2_out, not_3_out, not_4_out, not_5_out, not_6_out, not_7_out, not_8_out, or_1_out, or_2_out,
       or_3_out, or_4_out, or_5_out, or_6_out, or_7_out, or_8_out;
  wire [3:0] counter_1_q;
  wire [4:0] counter_2_q;
  wire [7:0] multiplexer_1_out, multiplexer_2_out, multiplexer_3_out, multiplexer_4_out, multiplexer_5_out,
       multiplexer_6_out, multiplexer_7_out, multiplexer_8_out, multiplexer_9_out, multiplexer_10_out,
       multiplexer_11_out, multiplexer_12_out, multiplexer_13_out, multiplexer_14_out, multiplexer_15_out,
       multiplexer_16_out, multiplexer_17_out, multiplexer_18_out;

  and and_1 (and_1_out, write, a_ok);
  and and_2 (and_2_out, write, b_ok);
  and and_3 (and_3_out, write, c_ok);
  and and_4 (and_4_out, write, d_ok);
  and and_5 (and_5_out, write, e_ok);
  and and_6 (and_6_out, write, f_ok);
  and and_7 (and_7_out, write, g_ok);
  and and_8 (and_8_out, write, h_ok);
  Multiplexer #(.width(8), .enable("false")) multiplexer_1 (
    .in0(8'h3), .in1(a), .out(multiplexer_1_out), .sel(and_1_out));
  Multiplexer #(.width(8), .enable("false")) multiplexer_2 (
    .in0(8'h3), .in1(b), .out(multiplexer_2_out), .sel(and_2_out));
  Multiplexer #(.width(8), .enable("false")) multiplexer_3 (
    .in0(8'h3), .in1(c), .out(multiplexer_3_out), .sel(and_3_out));
  Multiplexer #(.width(8), .enable("false")) multiplexer_4 (
    .in0(8'h3), .in1(d), .out(multiplexer_4_out), .sel(and_4_out));
  Multiplexer #(.width(8), .enable("false")) multiplexer_5 (
    .in0(8'h3), .in1(e), .out(multiplexer_5_out), .sel(and_5_out));
  Multiplexer #(.width(8), .enable("false")) multiplexer_6 (
    .in0(8'h3), .in1(f), .out(multiplexer_6_out), .sel(and_6_out));
  Multiplexer #(.width(8), .enable("false")) multiplexer_7 (
    .in0(8'h3), .in1(g), .out(multiplexer_7_out), .sel(and_7_out));
  Multiplexer #(.width(8), .enable("false")) multiplexer_8 (
    .in0(8'h3), .in1(h), .out(multiplexer_8_out), .sel(and_8_out));
  not not_1 (not_1_out, and_1_out);
  not not_2 (not_2_out, and_2_out);
  not not_3 (not_3_out, and_3_out);
  not not_4 (not_4_out, and_4_out);
  not not_5 (not_5_out, and_5_out);
  not not_6 (not_6_out, and_6_out);
  Multiplexer #(.width(8), .enable("false")) multiplexer_9 (
    .in0(8'h2a), .in1(multiplexer_1_out), .out(multiplexer_9_out), .sel(or_1_out));
  or or_1 (or_1_out, found_a, not_1_out);
  Multiplexer #(.width(8), .enable("false")) multiplexer_10 (
    .in0(8'h2a), .in1(multiplexer_2_out), .out(multiplexer_10_out), .sel(or_2_out));
  or or_2 (or_2_out, found_b, not_2_out);
  Multiplexer #(.width(8), .enable("false")) multiplexer_11 (
    .in0(8'h2a), .in1(multiplexer_3_out), .out(multiplexer_11_out), .sel(or_3_out));
  or or_3 (or_3_out, found_c, not_3_out);
  Multiplexer #(.width(8), .enable("false")) multiplexer_12 (
    .in0(8'h2a), .in1(multiplexer_4_out), .out(multiplexer_12_out), .sel(or_4_out));
  or or_4 (or_4_out, found_d, not_4_out);
  Multiplexer #(.width(8), .enable("false")) multiplexer_13 (
    .in0(8'h2a), .in1(multiplexer_5_out), .out(multiplexer_13_out), .sel(or_5_out));
  or or_5 (or_5_out, found_e, not_5_out);
  Multiplexer #(.width(8), .enable("false")) multiplexer_14 (
    .in0(8'h2a), .in1(multiplexer_6_out), .out(multiplexer_14_out), .sel(or_6_out));
  or or_6 (or_6_out, found_f, not_6_out);
  Multiplexer #(.width(8), .enable("false")) multiplexer_15 (
    .in0(8'h2a), .in1(multiplexer_7_out), .out(multiplexer_15_out), .sel(or_7_out));
  or or_7 (or_7_out, found_g, not_7_out);
  not not_7 (not_7_out, and_7_out);
  Multiplexer #(.width(8), .enable("false")) multiplexer_16 (
    .in0(8'h2a), .in1(multiplexer_8_out), .out(multiplexer_16_out), .sel(or_8_out));
  or or_8 (or_8_out, found_h, not_8_out);
  not not_8 (not_8_out, and_8_out);
  Multiplexer #(.select(4), .width(8), .enable("false")) multiplexer_17 (
    .in0(8'h3), .in1(8'h3), .in2(8'h3), .in3(8'h3), .in4(8'h3), .in5(8'h3), .in6(8'h3),
    .in7(multiplexer_9_out), .in8(multiplexer_10_out), .in9(multiplexer_11_out), .in10(multiplexer_12_out),
    .in11(multiplexer_13_out), .in12(multiplexer_14_out), .in13(multiplexer_15_out),
    .in14(multiplexer_16_out), .in15(8'ha), .out(multiplexer_17_out), .sel(counter_1_q));
  Counter #(.width(4), .max('hf), .ongoal("stay")) counter_1 (
    .count(write), .Q(counter_1_q), .carry(writing_is_done), .clk(clk), .clr(reset_write));  // open: load, D
  Multiplexer #(.select(5), .width(8), .enable("false")) multiplexer_18 (
    .in0(multiplexer_1_out), .in1(multiplexer_2_out), .in2(multiplexer_3_out), .in3(multiplexer_4_out),
    .in4(multiplexer_5_out), .in5(multiplexer_6_out), .in6(multiplexer_7_out), .in7(multiplexer_8_out),
    .in8(8'h3), .in9(8'h3), .in10(8'h3), .in11(8'h3), .in12(8'h3), .in13(8'h3), .in14(8'h3), .in15(8'h3),
    .in16(8'h3), .in17(8'h3), .in18(8'h3), .in19(8'h3), .in20(8'h3), .in21(8'h3), .in22(8'h3), .in23(8'h3),
    .in24(8'h3), .in25(8'h3), .in26(8'h3), .in27(8'h3), .in28(8'h3), .in29(8'h3), .in30(8'h3), .in31(8'ha),
    .out(multiplexer_18_out), .sel(counter_2_q));
  Counter #(.width(5), .max('h1f), .ongoal("stay")) counter_2 (
    .count(write_all_word), .Q(counter_2_q), .carry(writing_all_is_done), .clk(clk),
    .clr(reset_write_all_word));  // open: load, D
  Multiplexer #(.width(8), .enable("false")) multiplexer_19 (
    .in0(multiplexer_17_out), .in1(multiplexer_18_out), .out(current_letter), .sel(write_all_word));

  // Notes on the sheet:
  //   end_of_text
  //   star
endmodule

module getChoose (
  input  a,
  input  b,
  input  c,
  input  d,
  input  e,
  input  f,
  input  g,
  input  h,
  input  i,
  input  j,
  input  k,
  input  l,
  input  m,
  input  n,
  input  o,
  input  p,
  input  q,
  input  r,
  input  s,
  input  t,
  input  u,
  input  v,
  input  w,
  input  x,
  input  y,
  input  z,
  output [7:0] \input ,
  output is_input
);

  wire [4:0] controlled_buffer_1_out;

  assign controlled_buffer_1_out = a ? {5{1'b0}} : 5'bz;  // Controlled_Buffer controlled_buffer_1
  assign controlled_buffer_1_out = b ? 5'b00001 : 5'bz;  // Controlled_Buffer controlled_buffer_2
  assign controlled_buffer_1_out = c ? 5'b00010 : 5'bz;  // Controlled_Buffer controlled_buffer_3
  assign controlled_buffer_1_out = d ? 5'b00011 : 5'bz;  // Controlled_Buffer controlled_buffer_4
  assign controlled_buffer_1_out = e ? 5'b00100 : 5'bz;  // Controlled_Buffer controlled_buffer_5
  assign controlled_buffer_1_out = f ? 5'b00101 : 5'bz;  // Controlled_Buffer controlled_buffer_6
  assign controlled_buffer_1_out = h ? 5'b00111 : 5'bz;  // Controlled_Buffer controlled_buffer_7
  assign controlled_buffer_1_out = i ? 5'b01000 : 5'bz;  // Controlled_Buffer controlled_buffer_8
  assign controlled_buffer_1_out = j ? 5'b01001 : 5'bz;  // Controlled_Buffer controlled_buffer_9
  assign controlled_buffer_1_out = k ? 5'b01010 : 5'bz;  // Controlled_Buffer controlled_buffer_10
  assign controlled_buffer_1_out = l ? 5'b01011 : 5'bz;  // Controlled_Buffer controlled_buffer_11
  assign controlled_buffer_1_out = m ? 5'b01100 : 5'bz;  // Controlled_Buffer controlled_buffer_12
  assign controlled_buffer_1_out = n ? 5'b01101 : 5'bz;  // Controlled_Buffer controlled_buffer_13
  assign controlled_buffer_1_out = o ? 5'b01110 : 5'bz;  // Controlled_Buffer controlled_buffer_14
  assign controlled_buffer_1_out = p ? 5'b01111 : 5'bz;  // Controlled_Buffer controlled_buffer_15
  assign controlled_buffer_1_out = q ? 5'b10000 : 5'bz;  // Controlled_Buffer controlled_buffer_16
  assign controlled_buffer_1_out = r ? 5'b10001 : 5'bz;  // Controlled_Buffer controlled_buffer_17
  assign controlled_buffer_1_out = g ? 5'b00110 : 5'bz;  // Controlled_Buffer controlled_buffer_18
  assign controlled_buffer_1_out = s ? 5'b10010 : 5'bz;  // Controlled_Buffer controlled_buffer_19
  assign controlled_buffer_1_out = t ? 5'b10011 : 5'bz;  // Controlled_Buffer controlled_buffer_20
  assign controlled_buffer_1_out = u ? 5'b10100 : 5'bz;  // Controlled_Buffer controlled_buffer_21
  assign controlled_buffer_1_out = v ? 5'b10101 : 5'bz;  // Controlled_Buffer controlled_buffer_22
  assign controlled_buffer_1_out = w ? 5'b10110 : 5'bz;  // Controlled_Buffer controlled_buffer_23
  assign controlled_buffer_1_out = x ? 5'b10111 : 5'bz;  // Controlled_Buffer controlled_buffer_24
  assign controlled_buffer_1_out = y ? 5'b11000 : 5'bz;  // Controlled_Buffer controlled_buffer_25
  assign controlled_buffer_1_out = z ? 5'b11001 : 5'bz;  // Controlled_Buffer controlled_buffer_26
  or or_1 (is_input, a, b, c, d, e, g, h, i, j, f, k, l, m, n, o, p, q, r, s, z, t, u, y, v, w, x);
  Multiplexer #(.select(5), .width(8), .enable("false")) multiplexer_1 (
    .in0(8'h61), .in1(8'h62), .in2(8'h63), .in3(8'h64), .in4(8'h65), .in5(8'h66), .in6(8'h67), .in7(8'h68),
    .in8(8'h69), .in9(8'h6a), .in10(8'h6b), .in11(8'h6c), .in12(8'h6d), .in13(8'h6e), .in14(8'h6f),
    .in15(8'h70), .in16(8'h71), .in17(8'h72), .in18(8'h73), .in19(8'h74), .in20(8'h75), .in21(8'h76),
    .in22(8'h77), .in23(8'h78), .in24(8'h79), .in25(8'h7a), .out(\input ), .sel(controlled_buffer_1_out));  // open: in26, in27, in28, in29, in30, in31
endmodule

module hanging_man (
  input  [3:0] led_number,
  output [14:0] _8,
  output [14:0] _5,
  output [14:0] _6,
  output [14:0] _4,
  output [14:0] _3,
  output [14:0] _2,
  output [14:0] _7,
  output [14:0] _0,
  output [14:0] _1,
  output [14:0] _9
);

  Multiplexer #(.select(4), .width(15), .enable("false")) multiplexer_1 (
    .in0({15{1'b0}}), .in1(15'h1), .in2(15'h1), .in3(15'h1), .in4(15'h1), .in5(15'h1), .in6(15'h1),
    .in7(15'h1), .in8(15'h1), .in9(15'h1), .in10(15'h1), .in11(15'h1), .in12(15'h1), .in13(15'h1),
    .in14(15'h1), .in15(15'h1), .out(_1), .sel(led_number));
  Multiplexer #(.select(4), .width(15), .enable("false")) multiplexer_2 (
    .in0({15{1'b0}}), .in1(15'h1), .in2({15{1'b1}}), .in3({15{1'b1}}), .in4({15{1'b1}}), .in5({15{1'b1}}),
    .in6({15{1'b1}}), .in7({15{1'b1}}), .in8({15{1'b1}}), .in9({15{1'b1}}), .in10({15{1'b1}}), .out(_2),
    .sel(led_number));  // open: in11, in12, in13, in14, in15
  Multiplexer #(.select(4), .width(15), .enable("false")) multiplexer_3 (
    .in0({15{1'b0}}), .in1(15'h1), .in2(15'h1), .in3(15'h4001), .in4(15'h4001), .in5(15'h4001),
    .in6(15'h4001), .in7(15'h4001), .in8(15'h4001), .in9(15'h4001), .in10(15'h4001), .out(_3),
    .sel(led_number));  // open: in11, in12, in13, in14, in15
  Multiplexer #(.select(4), .width(15), .enable("false")) multiplexer_4 (
    .in0({15{1'b0}}), .in1(15'h1), .in2(15'h1), .in3(15'h4001), .in4(15'h4001), .in5(15'h4001),
    .in6(15'h4001), .in7(15'h4081), .in8(15'h4081), .in9(15'h4089), .in10(15'h4089), .out(_4),
    .sel(led_number));  // open: in11, in12, in13, in14, in15
  Multiplexer #(.select(4), .width(15), .enable("false")) multiplexer_5 (
    .in0({15{1'b0}}), .in1(15'h1), .in2(15'h1), .in3(15'h4001), .in4(15'h4001), .in5(15'h4401),
    .in6(15'h4401), .in7(15'h4501), .in8(15'h4501), .in9(15'h4511), .in10(15'h4511), .out(_5),
    .sel(led_number));  // open: in11, in12, in13, in14, in15
  Multiplexer #(.select(4), .width(15), .enable("false")) multiplexer_6 (
    .in0({15{1'b0}}), .in1(15'h1), .in2(15'h1), .in3(15'h4001), .in4(15'h7001), .in5(15'h7a01),
    .in6(15'h7bf9), .in7(15'h7bf9), .in8(15'h7bf9), .in9(15'h7bf9), .in10(15'h7bf9), .out(_6),
    .sel(led_number));  // open: in11, in12, in13, in14, in15
  Multiplexer #(.select(4), .width(15), .enable("false")) multiplexer_7 (
    .in0({15{1'b0}}), .in1(15'h1), .in2(15'h1), .in3(15'h1), .in4(15'h1), .in5(15'h401), .in6(15'h401),
    .in7(15'h401), .in8(15'h501), .in9(15'h501), .in10(15'h511), .out(_7), .sel(led_number));  // open: in11, in12, in13, in14, in15
  Multiplexer #(.select(4), .width(15), .enable("false")) multiplexer_8 (
    .in0({15{1'b0}}), .in1(15'h1), .in2(15'h1), .in3(15'h1), .in4(15'h1), .in5(15'h1), .in6(15'h1),
    .in7(15'h1), .in8(15'h81), .in9(15'h81), .in10(15'h89), .out(_8), .sel(led_number));  // open: in11, in12, in13, in14, in15

  assign _0 = {15{1'b0}};
  assign _9 = {15{1'b0}};

  // Notes on the sheet:
  //   1
  //   2
  //   3
  //   4
  //   5
  //   6
  //   7
  //   8
endmodule

module is_win (
  input  game_over,
  input  a_ok,
  input  is_in_a,
  input  b_ok,
  input  is_in_b,
  input  c_ok,
  input  is_in_c,
  input  d_ok,
  input  is_in_d,
  input  e_ok,
  input  is_in_e,
  input  f_ok,
  input  is_in_f,
  input  g_ok,
  input  is_in_g,
  input  h_ok,
  input  [8:0] number,
  input  is_in_h,
  input  clk,
  output [8:0] sum,
  output is_win,
  output b_res,
  output c_res,
  output d_res,
  output e_res,
  output f_res,
  output g_res,
  output h_res,
  output a_res
);

  wire adder_1_cout, adder_2_cout, adder_3_cout, adder_4_cout, adder_5_cout, adder_6_cout, and_1_out,
       and_2_out, and_3_out, and_4_out, and_5_out, and_6_out, and_7_out, and_8_out;
  wire [8:0] adder_1_out, adder_2_out, adder_3_out, adder_4_out, adder_5_out, adder_6_out,
       bit_extender_1_out, bit_extender_2_out, bit_extender_3_out, bit_extender_4_out, bit_extender_5_out,
       bit_extender_6_out, bit_extender_7_out, bit_extender_8_out;

  and and_1 (and_1_out, g_ok, is_in_g);
  and and_2 (and_2_out, h_ok, is_in_h);
  and and_3 (and_3_out, a_ok, is_in_a);
  and and_4 (and_4_out, b_ok, is_in_b);
  and and_5 (and_5_out, c_ok, is_in_c);
  and and_6 (and_6_out, d_ok, is_in_d);
  and and_7 (and_7_out, e_ok, is_in_e);
  and and_8 (and_8_out, f_ok, is_in_f);
  Register #(.width(1)) register_1 (.D(1'b1), .en(and_3_out), .Q(a_res), .clk(clk), .clr(game_over));
  Register #(.width(1)) register_2 (.D(1'b1), .en(and_4_out), .Q(b_res), .clk(clk), .clr(game_over));
  Register #(.width(1)) register_3 (.D(1'b1), .en(and_5_out), .Q(c_res), .clk(clk), .clr(game_over));
  Register #(.width(1)) register_4 (.D(1'b1), .en(and_6_out), .Q(d_res), .clk(clk), .clr(game_over));
  Register #(.width(1)) register_5 (.D(1'b1), .en(and_7_out), .Q(e_res), .clk(clk), .clr(game_over));
  Register #(.width(1)) register_6 (.D(1'b1), .en(and_8_out), .Q(f_res), .clk(clk), .clr(game_over));
  Register #(.width(1)) register_7 (.D(1'b1), .en(and_1_out), .Q(g_res), .clk(clk), .clr(game_over));
  Register #(.width(1)) register_8 (.D(1'b1), .en(and_2_out), .Q(h_res), .clk(clk), .clr(game_over));
  assign bit_extender_1_out = {{8{1'b0}}, a_res};  // Bit_Extender bit_extender_1
  assign bit_extender_2_out = {{8{1'b0}}, b_res};  // Bit_Extender bit_extender_2
  assign bit_extender_3_out = {{8{1'b0}}, c_res};  // Bit_Extender bit_extender_3
  assign bit_extender_4_out = {{8{1'b0}}, d_res};  // Bit_Extender bit_extender_4
  assign bit_extender_5_out = {{8{1'b0}}, e_res};  // Bit_Extender bit_extender_5
  assign bit_extender_6_out = {{8{1'b0}}, f_res};  // Bit_Extender bit_extender_6
  assign bit_extender_7_out = {{8{1'b0}}, g_res};  // Bit_Extender bit_extender_7
  assign bit_extender_8_out = {{8{1'b0}}, h_res};  // Bit_Extender bit_extender_8
  Adder #(.width(9)) adder_1 (
    .a(bit_extender_1_out), .b(bit_extender_2_out), .out(adder_1_out), .cout(adder_1_cout));  // open: cin
  Adder #(.width(9)) adder_2 (
    .a(adder_1_out), .b(bit_extender_3_out), .out(adder_2_out), .cin(adder_1_cout), .cout(adder_2_cout));
  Adder #(.width(9)) adder_3 (
    .a(adder_2_out), .b(bit_extender_4_out), .out(adder_3_out), .cin(adder_2_cout), .cout(adder_3_cout));
  Adder #(.width(9)) adder_4 (
    .a(adder_3_out), .b(bit_extender_5_out), .out(adder_4_out), .cin(adder_3_cout), .cout(adder_4_cout));
  Adder #(.width(9)) adder_5 (
    .a(adder_4_out), .b(bit_extender_6_out), .out(adder_5_out), .cin(adder_4_cout), .cout(adder_5_cout));
  Adder #(.width(9)) adder_6 (
    .a(adder_5_out), .b(bit_extender_7_out), .out(adder_6_out), .cin(adder_5_cout), .cout(adder_6_cout));
  Adder #(.width(9)) adder_7 (.a(adder_6_out), .b(bit_extender_8_out), .out(sum), .cin(adder_6_cout));  // open: cout
  Comparator #(.width(9)) comparator_1 (.a(sum), .b(number), .eq(is_win));  // open: gt, lt
endmodule

// Control_Unit
module control_unit (
  input  start,
  input  is_win,
  input  is_lost,
  input  fail,
  input  \input ,
  input  writing_is_done,
  input  writing_all_is_done,
  input  go,
  input  clk,
  output write,
  output write_reset,
  output machine_win,
  output game_over,
  output load_number,
  output increment_led,
  output load_sum,
  output user_win,
  output load_input
);

  wire and_1_out, and_2_out, and_3_out, and_7_out, and_8_out, and_9_out, and_10_out, and_11_out, and_12_out,
       and_13_out, and_15_out, and_16_out, and_17_out, and_18_out, and_19_out, and_20_out, and_21_out,
       and_22_out, and_23_out, and_24_out, and_25_out, and_26_out, and_27_out, and_28_out, and_29_out,
       and_30_out, and_31_out, and_32_out, and_33_out, and_35_out, not_1_out, not_2_out, not_3_out,
       not_4_out, not_5_out, not_6_out, not_7_out, not_8_out, not_9_out, not_10_out, not_11_out, not_12_out,
       not_13_out, not_14_out, not_15_out, not_16_out, not_17_out, not_18_out, not_19_out, not_20_out,
       not_21_out, not_22_out, not_23_out, not_24_out, not_25_out, not_26_out, not_27_out, not_28_out,
       not_29_out, not_30_out, not_31_out, not_32_out, not_33_out, not_34_out, not_35_out, not_36_out,
       not_37_out, not_38_out, not_39_out, not_40_out, not_41_out, not_42_out, not_43_out, not_44_out,
       not_45_out, not_46_out, not_47_out, not_48_out, not_49_out, not_50_out, not_51_out, not_52_out,
       not_53_out, not_54_out, not_55_out, not_56_out, not_57_out, not_58_out, not_59_out, not_60_out,
       not_61_out, not_62_out, not_63_out, not_64_out, not_65_out, not_66_out, not_67_out, not_68_out,
       not_69_out;
  wire [3:0] or_5_out, state_q;

  not not_1 (not_1_out, state_q[2]);
  not not_2 (not_2_out, state_q[1]);
  not not_3 (not_3_out, state_q[0]);
  Register #(.width(4)) state (.D(or_5_out), .en(1'b1), .Q(state_q), .clk(clk));  // open: clr
  not not_4 (not_4_out, state_q[3]);
  and and_1 (and_1_out, not_4_out, state_q[2], state_q[1]);
  and and_2 (and_2_out, not_4_out, not_1_out, not_2_out, state_q[0]);
  and and_3 (and_3_out, state_q[3], not_1_out, not_2_out, not_3_out);
  not not_5 (not_5_out, state_q[3]);
  not not_6 (not_6_out, state_q[0]);
  not not_7 (not_7_out, state_q[2]);
  not not_8 (not_8_out, state_q[1]);
  not not_9 (not_9_out, state_q[0]);
  not not_10 (not_10_out, writing_all_is_done);
  or or_1 (write, and_1_out, and_3_out, and_2_out, load_number);
  not not_11 (not_11_out, state_q[3]);
  not not_12 (not_12_out, is_win);
  not not_13 (not_13_out, state_q[2]);
  not not_14 (not_14_out, state_q[2]);
  not not_15 (not_15_out, state_q[2]);
  and and_4 (machine_win, not_15_out, not_16_out, not_17_out, state_q[3]);
  not not_16 (not_16_out, state_q[1]);
  not not_17 (not_17_out, state_q[0]);
  not not_18 (not_18_out, state_q[3]);
  and and_5 (load_number, not_1_out, not_2_out, state_q[0], not_5_out);
  and and_6 (increment_led, state_q[2], not_2_out, state_q[0], not_5_out);
  and and_7 (and_7_out, state_q[2], state_q[1], not_6_out, not_5_out);
  not not_19 (not_19_out, state_q[3]);
  and and_8 (and_8_out, not_11_out, not_7_out, state_q[1], not_9_out);
  and and_9 (and_9_out, not_12_out, is_lost);
  and and_10 (and_10_out, state_q[3], not_13_out, not_8_out, not_9_out);
  not not_20 (not_20_out, state_q[3]);
  not not_21 (not_21_out, state_q[2]);
  not not_22 (not_22_out, state_q[1]);
  not not_23 (not_23_out, state_q[0]);
  not not_24 (not_24_out, state_q[3]);
  not not_25 (not_25_out, state_q[2]);
  not not_26 (not_26_out, state_q[1]);
  not not_27 (not_27_out, writing_is_done);
  not not_28 (not_28_out, state_q[3]);
  not not_29 (not_29_out, state_q[2]);
  not not_30 (not_30_out, state_q[0]);
  not not_31 (not_31_out, is_lost);
  not not_32 (not_32_out, state_q[3]);
  not not_33 (not_33_out, state_q[2]);
  not not_34 (not_34_out, \input );
  not not_35 (not_35_out, state_q[3]);
  not not_36 (not_36_out, state_q[1]);
  not not_37 (not_37_out, state_q[0]);
  not not_38 (not_38_out, state_q[3]);
  not not_39 (not_39_out, state_q[2]);
  not not_40 (not_40_out, state_q[0]);
  not not_41 (not_41_out, is_lost);
  not not_42 (not_42_out, state_q[3]);
  not not_43 (not_43_out, state_q[2]);
  not not_44 (not_44_out, state_q[3]);
  not not_45 (not_45_out, state_q[1]);
  not not_46 (not_46_out, state_q[0]);
  not not_47 (not_47_out, state_q[3]);
  not not_48 (not_48_out, state_q[0]);
  not not_49 (not_49_out, writing_is_done);
  not not_50 (not_50_out, state_q[3]);
  not not_51 (not_51_out, writing_all_is_done);
  and and_11 (and_11_out, not_14_out, state_q[1], state_q[0], not_4_out);
  and and_12 (and_12_out, not_18_out, state_q[2], state_q[1], state_q[0]);
  and and_13 (and_13_out, not_2_out, state_q[2], state_q[0], not_5_out);
  and and_14 (user_win, state_q[2], state_q[1], not_19_out, state_q[0]);
  and and_15 (and_15_out, not_20_out, not_21_out, not_22_out, not_23_out, start);
  and and_16 (and_16_out, not_24_out, not_25_out, not_26_out, state_q[0], not_27_out);
  and and_17 (and_17_out, not_28_out, not_29_out, state_q[1], not_30_out, not_31_out);
  and and_18 (and_18_out, not_32_out, not_33_out, state_q[1], state_q[0], not_34_out);
  and and_19 (and_19_out, not_35_out, state_q[2], not_36_out, not_37_out, go, fail);
  not not_52 (not_52_out, state_q[3]);
  not not_53 (not_53_out, state_q[1]);
  not not_54 (not_54_out, state_q[3]);
  not not_55 (not_55_out, state_q[0]);
  not not_56 (not_56_out, is_lost);
  not not_57 (not_57_out, state_q[3]);
  not not_58 (not_58_out, state_q[2]);
  not not_59 (not_59_out, \input );
  not not_60 (not_60_out, state_q[3]);
  not not_61 (not_61_out, state_q[0]);
  not not_62 (not_62_out, fail);
  not not_63 (not_63_out, state_q[3]);
  not not_64 (not_64_out, state_q[1]);
  not not_65 (not_65_out, state_q[3]);
  not not_66 (not_66_out, state_q[0]);
  not not_67 (not_67_out, state_q[3]);
  not not_68 (not_68_out, writing_all_is_done);
  and and_20 (and_20_out, not_38_out, not_39_out, state_q[1], not_40_out, is_win, not_41_out);
  and and_21 (and_21_out, not_42_out, not_43_out, state_q[1], state_q[0], \input );
  and and_22 (and_22_out, not_44_out, state_q[2], not_45_out, not_46_out);
  and and_23 (and_23_out, not_47_out, state_q[2], not_48_out, not_49_out);
  and and_24 (and_24_out, not_50_out, state_q[2], state_q[1], state_q[0], not_51_out);
  or or_2 (write_reset, and_11_out, game_over);
  or or_3 (game_over, machine_win, and_12_out);
  or or_4 (load_sum, and_7_out, and_13_out);
  and and_25 (and_25_out, and_8_out, and_9_out);
  and and_26 (and_26_out, and_10_out, not_10_out);
  or or_5 (or_5_out[0], and_35_out, and_15_out, and_16_out, and_17_out, and_18_out, and_19_out);
  and and_27 (and_27_out, not_52_out, not_53_out, state_q[0], writing_is_done);
  and and_28 (and_28_out, not_54_out, state_q[1], not_55_out, not_56_out);
  and and_29 (and_29_out, not_57_out, not_58_out, state_q[1], state_q[0], not_59_out);
  and and_30 (and_30_out, not_60_out, state_q[2], not_61_out, not_62_out, go);
  and and_31 (and_31_out, not_63_out, state_q[2], not_64_out, state_q[0]);
  and and_32 (and_32_out, not_65_out, state_q[2], state_q[1], not_66_out);
  and and_33 (and_33_out, not_67_out, state_q[2], state_q[1], not_68_out);
  or or_6 (or_5_out[2], and_20_out, and_21_out, and_22_out, and_23_out, and_24_out);
  and and_34 (load_input, not_19_out, state_q[2], not_69_out, not_9_out);
  not not_69 (not_69_out, state_q[1]);
  or or_7 (or_5_out[3], and_25_out, and_26_out);
  and and_35 (and_35_out, not_11_out, state_q[2], state_q[1], state_q[0], not_10_out);
  or or_8 (or_5_out[1], and_27_out, and_28_out, and_29_out, and_30_out, and_31_out, and_32_out, and_33_out);
endmodule
