// Logisim project 171044098.circ as structural Verilog: 1 circuit, main circuit main
module main (
  input  a,
  input  b,
  input  c,
  input  d,
  input  e,
  output result
);

  wire and_1_out, and_2_out, and_3_out, and_4_out, and_5_out, and_6_out, and_7_out, and_8_out, and_9_out,
       and_10_out, and_11_out, and_12_out, and_13_out, and_14_out, and_15_out, and_16_out, and_17_out,
       and_18_out, not_1_out, not_2_out, not_3_out, not_4_out, not_5_out, not_6_out, not_7_out, not_8_out,
       not_9_out, not_10_out, not_11_out, or_1_out, or_2_out, or_3_out;

  not not_1 (not_1_out, a);
  not not_2 (not_2_out, b);
  not not_3 (not_3_out, b);
  not not_4 (not_4_out, a);
  not not_5 (not_5_out, b);
  and and_1 (and_1_out, not_1_out, not_2_out);
  and and_2 (and_2_out, c, e);
  and and_3 (and_3_out, not_3_out, c);
  and and_4 (and_4_out, d, e);
  and and_5 (and_5_out, not_4_out, b);
  not not_6 (not_6_out, e);
  and and_6 (and_6_out, a, not_5_out);
  not not_7 (not_7_out, c);
  not not_8 (not_8_out, d);
  not not_9 (not_9_out, e);
  and and_7 (and_7_out, a, b);
  not not_10 (not_10_out, c);
  not not_11 (not_11_out, d);
  and and_8 (and_8_out, and_1_out, and_2_out);
  or or_1 (or_1_out, and_8_out, and_9_out);
  and and_9 (and_9_out, and_3_out, and_4_out);
  and and_10 (and_10_out, and_5_out, c);
  and and_11 (and_11_out, and_10_out, and_12_out);
  and and_12 (and_12_out, d, not_6_out);
  and and_13 (and_13_out, and_6_out, not_7_out);
  and and_14 (and_14_out, and_13_out, and_15_out);
  and and_15 (and_15_out, not_8_out, not_9_out);
  and and_16 (and_16_out, and_7_out, not_10_out);
  and and_17 (and_17_out, and_16_out, and_18_out);
  and and_18 (and_18_out, not_11_out, e);
  or or_2 (or_2_out, or_1_out, and_11_out);
  or or_3 (or_3_out, and_14_out, and_17_out);
  or or_4 (result, or_2_out, or_3_out);
endmodule
