// Logisim project 171044098_lab3.circ as structural Verilog: 1 circuit, main circuit main
module main (
  input  a,
  input  b
);

  wire and_1_out, and_2_out, and_3_out, and_4_out, and_5_out, and_6_out, and_7_out, and_8_out, and_9_out,
       and_10_out, clock_1_out, not_1_out, not_2_out, not_3_out, not_4_out, not_5_out, not_6_out, or_2_out;
  wire [1:0] or_3_out, state_q;

  Clock clock_1 (.out(clock_1_out));
  not not_1 (not_1_out, state_q[1]);
  Register #(.width(2)) state (.D(or_3_out), .en(1'b1), .Q(state_q), .clk(clock_1_out));  // open: clr
  not not_2 (not_2_out, a);
  not not_3 (not_3_out, b);
  not not_4 (not_4_out, state_q[0]);
  and and_1 (and_1_out, not_1_out, state_q[0], a);
  and and_2 (and_2_out, state_q[1], state_q[0], b);
  and and_3 (and_3_out, state_q[1], not_4_out, not_2_out);
  and and_4 (and_4_out, state_q[1], not_4_out, a, b);
  not not_5 (not_5_out, state_q[1]);
  not not_6 (not_6_out, state_q[1]);
  and and_5 (and_5_out, state_q[1], state_q[0], a);
  and and_6 (and_6_out, state_q[1], not_4_out, b, not_2_out);
  and and_7 (and_7_out, not_5_out, state_q[0], b, not_3_out);
  and and_8 (and_8_out, not_6_out, not_4_out, a, not_3_out);
  or or_1 (or_3_out[1], and_1_out, and_2_out, and_3_out, and_4_out);
  and and_9 (and_9_out, state_q[1], not_4_out);
  and and_10 (and_10_out, state_q[1], state_q[0]);
  or or_2 (or_2_out, and_9_out, and_10_out);
  or or_3 (or_3_out[0], and_5_out, and_6_out, and_7_out, and_8_out);
  LED x (.in(or_2_out));
endmodule
