// Logisim project 171044098.circ as structural Verilog: 1 circuit, main circuit main
module main (
  input  req,
  input  p3s,
  input  p7s,
  input  p37s
);

  wire and_1_out, and_2_out, and_3_out, and_4_out, and_5_out, and_6_out, and_7_out, and_8_out, and_9_out,
       and_10_out, and_11_out, and_12_out, and_13_out, and_14_out, and_15_out, clock_1_out, not_1_out,
       not_2_out, not_3_out, not_4_out, not_5_out, not_6_out, or_1_out, or_4_out, or_5_out, or_6_out;
  wire [1:0] or_3_out, state_q;

  Clock clock_1 (.out(clock_1_out));
  not not_1 (not_1_out, state_q[1]);
  not not_2 (not_2_out, state_q[0]);
  Register #(.width(2)) state (.D(or_3_out), .en(1'b1), .Q(state_q), .clk(clock_1_out));  // open: clr
  not not_3 (not_3_out, req);
  not not_4 (not_4_out, p3s);
  not not_5 (not_5_out, p7s);
  not not_6 (not_6_out, p37s);
  and and_1 (and_1_out, state_q[1], not_2_out);
  and and_2 (and_2_out, not_1_out, not_2_out, req, not_6_out);
  and and_3 (and_3_out, not_1_out, state_q[0], not_3_out);
  and and_4 (and_4_out, state_q[1], state_q[0], not_6_out);
  and and_5 (and_5_out, state_q[1], not_2_out, p7s);
  and and_6 (and_6_out, state_q[1], state_q[0], not_6_out);
  and and_7 (and_7_out, not_1_out, req, p3s);
  and and_8 (and_8_out, state_q[1], p7s, not_2_out);
  and and_9 (and_9_out, state_q[1], state_q[0], p37s);
  or or_1 (or_1_out, and_2_out, and_8_out, and_9_out);
  LED led_1 (.in(or_1_out));
  or or_2 (or_3_out[1], and_3_out, and_1_out, and_4_out);
  or or_3 (or_3_out[0], and_5_out, and_6_out, and_7_out);
  and and_10 (and_10_out, req, p3s, not_1_out);
  and and_11 (and_11_out, not_1_out, not_2_out);
  and and_12 (and_12_out, not_1_out, state_q[0], not_3_out);
  and and_13 (and_13_out, state_q[1], not_2_out, not_5_out);
  or or_4 (or_4_out, and_10_out, and_11_out);
  and and_14 (and_14_out, state_q[1], not_2_out, p7s);
  and and_15 (and_15_out, state_q[1], state_q[0], not_6_out);
  LED led_2 (.in(or_4_out));
  or or_5 (or_5_out, and_12_out, and_13_out);
  LED led_3 (.in(or_5_out));
  or or_6 (or_6_out, and_14_out, and_15_out);
  LED led_4 (.in(or_6_out));

  // Notes on the sheet:
  //   resetT
  //   redL
  //   orange
  //   green
endmodule
