// Logisim project 171044098_lab5.circ as structural Verilog: 3 circuits, main circuit 171044098
module main (
  input  req,
  input  p3s,
  input  p7s,
  input  p37s,
  input  clk,
  output red,
  output orange,
  output green,
  output resetT
);

  wire and_1_out, and_2_out, and_3_out, and_4_out, and_5_out, and_6_out, and_7_out, and_10_out, and_11_out,
       not_1_out, not_2_out, not_3_out, not_5_out;
  wire [1:0] or_2_out, state_q;

  Register #(.width(2)) state (.D(or_2_out), .en(1'b1), .Q(state_q), .clk(clk));  // open: clr
  not not_1 (not_1_out, state_q[1]);
  not not_2 (not_2_out, state_q[0]);
  not not_3 (not_3_out, p3s);
  // NOT_Gate not_4 has open pins: in=p7s, out=open
  not not_5 (not_5_out, p37s);
  and and_1 (and_1_out, p3s, not_1_out, state_q[0]);
  and and_2 (and_2_out, not_5_out, state_q[1], state_q[0]);
  and and_3 (and_3_out, state_q[1], not_2_out);
  and and_4 (and_4_out, req, not_1_out, not_2_out);
  and and_5 (and_5_out, not_3_out, not_1_out, state_q[0]);
  and and_6 (and_6_out, state_q[1], p7s, not_2_out);
  and and_7 (and_7_out, not_5_out, state_q[1], state_q[0]);
  or or_1 (or_2_out[1], and_1_out, and_2_out, and_3_out);
  or or_2 (or_2_out[0], and_4_out, and_5_out, and_6_out, and_7_out);
  and and_8 (orange, state_q[1], not_2_out);
  and and_9 (green, state_q[1], state_q[0]);
  and and_10 (and_10_out, not_1_out, not_2_out);
  and and_11 (and_11_out, not_1_out, state_q[0]);
  and and_12 (resetT, not_1_out, not_2_out);
  or or_3 (red, and_10_out, and_11_out);

  // Notes on the sheet:
  //   n1
  //   n0
endmodule

module _171044098 (
);

  wire button_1_out, clock_1_out, control_unit_green, control_unit_orange, control_unit_red,
       control_unit_resett, datapath__3, datapath__7, datapath__37;

  Clock clock_1 (.out(clock_1_out));
  Button button_1 (.out(button_1_out));
  datapath datapath (
    .clock(clock_1_out), ._3(datapath__3), ._7(datapath__7), ._37(datapath__37), .reset(control_unit_resett));
  main control_unit (
    .req(button_1_out), .p3s(datapath__3), .p7s(datapath__7), .p37s(datapath__37), .clk(clock_1_out),
    .red(control_unit_red), .orange(control_unit_orange), .green(control_unit_green),
    .resetT(control_unit_resett));
  LED led_1 (.in(control_unit_red));
  LED led_2 (.in(control_unit_orange));
  LED led_3 (.in(control_unit_green));
  LED led_4 (.in(control_unit_resett));

  // Notes on the sheet:
  //   req
  //   red
  //   orange
  //   green
  //   reset
endmodule

module datapath (
  input  clock,
  input  reset,
  output _3,
  output _7,
  output _37
);

  wire [5:0] counter_q;

  Counter #(.width(6), .max('h37)) counter (
    .count(1'b1), .Q(counter_q), .clk(clock), .clr(reset));  // open: load, D, carry
  Comparator #(.width(6)) comparator_1 (.a(counter_q), .b(6'b000011), .eq(_3));  // open: gt, lt
  Comparator #(.width(6)) comparator_2 (.a(counter_q), .b(6'b000111), .eq(_7));  // open: gt, lt
  Comparator #(.width(6)) comparator_3 (.a(counter_q), .b(6'b100101), .eq(_37));  // open: gt, lt

  // Notes on the sheet:
  //   counter
endmodule
