// Logisim project 171044098_lab6.circ as structural Verilog: 3 circuits, main circuit main
module main (
  input  [7:0] x,
  input  [7:0] y,
  input  [7:0] z,
  output [7:0] out_4
);

  wire button_1_out, clock_1_out, control_unit_load, control_unit_lres, control_unit_select, datapath_big,
       datapath_eq, datapath_less;

  Clock clock_1 (.out(clock_1_out));
  // Probe on x
  // Probe on y
  // Probe on z
  // Probe on out_4
  datapath datapath (
    .Lres(control_unit_lres), .x(x), .y(y), .z(z), .Select(control_unit_select), .Load(control_unit_load),
    .clk(clock_1_out), .res(out_4), .big(datapath_big), .eq(datapath_eq), .less(datapath_less));
  Button button_1 (.out(button_1_out));
  control_unit control_unit (
    .big(datapath_big), .eq(datapath_eq), .go(button_1_out), .less(datapath_less), .clk(clock_1_out),
    .Load(control_unit_load), .select(control_unit_select), .Lres(control_unit_lres));

  // Notes on the sheet:
  //   result
endmodule

module control_unit (
  input  big,
  input  eq,
  input  go,
  input  less,
  input  clk,
  output Load,
  output select,
  output Lres
);

  wire and_4_out, and_5_out, and_6_out, and_7_out, not_1_out, not_2_out, not_3_out, not_4_out, not_5_out,
       not_6_out;
  wire [2:0] or_2_out, state_q;

  not not_1 (not_1_out, state_q[2]);
  not not_2 (not_2_out, state_q[1]);
  not not_3 (not_3_out, state_q[0]);
  Register #(.width(3)) state (.D(or_2_out), .en(1'b1), .Q(state_q), .clk(clk));  // open: clr
  not not_4 (not_4_out, big);
  not not_5 (not_5_out, eq);
  not not_6 (not_6_out, go);
  and and_1 (Load, not_1_out, state_q[0]);
  and and_2 (select, not_1_out, state_q[1], state_q[0]);
  and and_3 (Lres, state_q[2], not_2_out, not_3_out);
  and and_4 (and_4_out, not_1_out, state_q[1], not_3_out, eq);
  and and_5 (and_5_out, not_1_out, state_q[1], not_3_out, big);
  and and_6 (and_6_out, not_1_out, not_2_out, not_3_out, go);
  or or_1 (or_2_out[1], Load, and_5_out);
  or or_2 (or_2_out[0], and_5_out, and_6_out);
  and and_7 (and_7_out, not_1_out, state_q[1], not_3_out, less);
  or or_3 (or_2_out[2], and_7_out, and_4_out);

  // Notes on the sheet:
  //   n2
  //   n1
  //   n0
endmodule

module datapath (
  input  Lres,
  input  [7:0] x,
  input  [7:0] y,
  input  [7:0] z,
  input  Select,
  input  Load,
  input  clk,
  output [7:0] res,
  output big,
  output eq,
  output less
);

  wire [7:0] diff2_q, diff_q, multiplexer_1_out, multiplexer_2_out, multiplier_1_out, subtractor_1_out,
       subtractor_2_out, z_q;

  Subtractor subtractor_1 (.a(x), .b(y), .out(subtractor_1_out));  // open: bin, bout
  Multiplexer #(.width(8), .enable("false")) multiplexer_1 (
    .in0(z), .in1(multiplier_1_out), .out(multiplexer_1_out), .sel(Select));
  Multiplexer #(.width(8), .enable("false")) multiplexer_2 (
    .in0(subtractor_1_out), .in1(subtractor_2_out), .out(multiplexer_2_out), .sel(Select));
  Register u_z (.D(multiplexer_1_out), .en(Load), .Q(z_q), .clk(clk));  // open: clr
  Register diff (.D(multiplexer_2_out), .en(Load), .Q(diff_q), .clk(clk));  // open: clr
  Register register_1 (.D(z_q), .en(Lres), .Q(res), .clk(clk));  // open: clr
  Register diff2 (.D(multiplexer_2_out), .en(Load), .Q(diff2_q), .clk(clk));  // open: clr
  Multiplier multiplier_1 (.a(z_q), .b(diff2_q), .out(multiplier_1_out));  // open: cin, cout
  Comparator comparator_1 (.a(diff_q), .b({8{1'b0}}), .gt(big), .eq(eq), .lt(less));
  Subtractor subtractor_2 (.a(diff_q), .b(8'h1), .out(subtractor_2_out));  // open: bin, bout
endmodule
