// Logisim project full.circ as structural Verilog: 3 circuits, main circuit game
module Control_Unit (
  input  b1,
  input  reset,
  input  b2,
  input  clk,
  output a,
  output b,
  output c,
  output d,
  output e,
  output f,
  output g,
  output b1_win,
  output b2_win
);

  wire and_2_out, and_3_out, and_4_out, and_5_out, and_6_out, and_7_out, and_9_out, and_10_out, and_11_out,
       and_12_out, and_13_out, and_14_out, and_15_out, and_16_out, and_17_out, and_18_out, and_19_out,
       and_20_out, and_21_out, and_22_out, and_23_out, and_24_out, and_25_out, and_26_out, and_27_out,
       and_28_out, and_29_out, and_30_out, and_31_out, and_32_out, and_33_out, and_34_out, and_35_out,
       and_36_out, and_37_out, and_38_out, and_39_out, and_40_out, and_41_out, and_42_out, and_43_out,
       and_44_out, and_45_out, and_46_out, and_47_out, and_48_out, and_49_out, and_50_out, not_1_out,
       not_2_out, not_3_out, not_4_out, not_5_out, not_6_out, not_7_out, not_8_out, not_9_out, not_10_out,
       not_11_out, not_12_out, not_13_out, not_14_out, not_15_out, not_16_out, not_17_out, not_18_out,
       not_19_out, not_20_out, not_21_out, not_22_out, not_23_out, not_24_out, not_25_out, not_26_out,
       not_27_out, not_28_out, not_29_out, not_30_out, not_31_out, not_32_out, not_33_out, not_34_out,
       not_35_out, not_36_out, not_37_out, not_38_out, not_39_out, not_40_out, not_41_out, not_42_out,
       not_43_out, not_44_out, not_45_out, not_46_out, not_47_out, not_48_out, not_49_out, not_50_out,
       not_51_out, not_52_out, not_53_out, not_54_out, not_55_out, not_56_out, not_57_out, not_58_out,
       not_59_out, not_60_out, not_61_out, not_62_out, not_63_out, not_64_out, not_65_out, not_66_out,
       not_67_out, not_68_out, not_69_out, not_70_out, not_71_out, not_72_out, not_73_out, not_74_out,
       not_75_out, not_76_out, not_77_out, not_78_out, not_79_out, not_80_out, not_81_out, not_82_out,
       not_83_out, not_84_out, not_85_out, not_86_out, not_87_out, not_88_out, not_89_out, not_90_out,
       not_91_out, not_92_out, not_93_out, not_94_out, not_95_out, not_96_out, not_97_out, not_98_out,
       not_99_out, not_100_out, not_101_out, not_102_out, not_103_out, not_104_out, not_105_out, not_106_out,
       not_107_out, not_108_out, not_109_out, not_110_out, not_111_out, not_112_out, not_113_out,
       not_114_out, not_115_out, not_116_out, not_117_out, not_118_out, not_119_out, not_120_out,
       not_121_out, not_122_out, not_123_out, not_124_out, not_125_out, not_126_out, not_127_out,
       not_128_out, not_129_out, not_130_out, not_131_out, not_132_out;
  wire [3:0] or_9_out, State_q;

  Register #(.width(4)) State (.D(or_9_out), .en(1'b1), .Q(State_q), .clk(clk));  // open: clr
  not not_1 (not_1_out, State_q[3]);
  not not_2 (not_2_out, State_q[0]);
  not not_3 (not_3_out, State_q[3]);
  not not_4 (not_4_out, State_q[2]);
  not not_5 (not_5_out, State_q[1]);
  not not_6 (not_6_out, State_q[0]);
  and and_1 (b2_win, not_1_out, State_q[2], State_q[1], not_2_out);
  not not_7 (not_7_out, State_q[3]);
  not not_8 (not_8_out, State_q[2]);
  not not_9 (not_9_out, State_q[3]);
  not not_10 (not_10_out, State_q[1]);
  not not_11 (not_11_out, State_q[0]);
  not not_12 (not_12_out, State_q[3]);
  not not_13 (not_13_out, State_q[2]);
  not not_14 (not_14_out, State_q[1]);
  not not_15 (not_15_out, State_q[3]);
  not not_16 (not_16_out, State_q[2]);
  not not_17 (not_17_out, State_q[0]);
  and and_2 (and_2_out, not_3_out, State_q[2], State_q[1], State_q[0]);
  and and_3 (and_3_out, State_q[3], not_4_out, not_5_out, not_6_out);
  not not_18 (not_18_out, State_q[1]);
  not not_19 (not_19_out, State_q[3]);
  and and_4 (and_4_out, not_7_out, not_8_out, State_q[1], State_q[0]);
  and and_5 (and_5_out, not_9_out, State_q[2], not_10_out, not_11_out);
  and and_6 (and_6_out, not_12_out, not_13_out, not_14_out, State_q[0]);
  and and_7 (and_7_out, not_15_out, not_16_out, State_q[1], not_17_out);
  not not_20 (not_20_out, State_q[3]);
  not not_21 (not_21_out, State_q[2]);
  not not_22 (not_22_out, State_q[1]);
  not not_23 (not_23_out, State_q[0]);
  not not_24 (not_24_out, State_q[2]);
  not not_25 (not_25_out, State_q[2]);
  not not_26 (not_26_out, State_q[1]);
  not not_27 (not_27_out, State_q[2]);
  not not_28 (not_28_out, State_q[0]);
  or or_1 (f, and_2_out, and_3_out);
  and and_8 (a, State_q[0], not_18_out, State_q[2], not_19_out);
  or or_2 (b, and_4_out, and_5_out);
  or or_3 (c, and_6_out, and_7_out);
  and and_9 (and_9_out, not_20_out, not_21_out, not_22_out, not_23_out);
  and and_10 (and_10_out, State_q[3], not_24_out, State_q[1], State_q[0]);
  and and_11 (and_11_out, State_q[3], not_25_out, not_26_out, State_q[0]);
  and and_12 (and_12_out, State_q[3], not_27_out, State_q[1], not_28_out);
  or or_4 (d, and_9_out, and_10_out);
  or or_5 (e, and_11_out, and_12_out);
  not not_29 (not_29_out, State_q[3]);
  not not_30 (not_30_out, State_q[2]);
  not not_31 (not_31_out, State_q[0]);
  not not_32 (not_32_out, b1);
  not not_33 (not_33_out, reset);
  not not_34 (not_34_out, State_q[3]);
  not not_35 (not_35_out, State_q[2]);
  not not_36 (not_36_out, State_q[1]);
  not not_37 (not_37_out, b2);
  not not_38 (not_38_out, b1);
  not not_39 (not_39_out, reset);
  not not_40 (not_40_out, State_q[3]);
  not not_41 (not_41_out, State_q[0]);
  not not_42 (not_42_out, reset);
  not not_43 (not_43_out, State_q[3]);
  not not_44 (not_44_out, State_q[2]);
  not not_45 (not_45_out, State_q[3]);
  not not_46 (not_46_out, State_q[2]);
  not not_47 (not_47_out, State_q[3]);
  not not_48 (not_48_out, reset);
  not not_49 (not_49_out, State_q[2]);
  not not_50 (not_50_out, State_q[1]);
  not not_51 (not_51_out, State_q[0]);
  not not_52 (not_52_out, b2);
  not not_53 (not_53_out, b1);
  not not_54 (not_54_out, reset);
  not not_55 (not_55_out, State_q[2]);
  not not_56 (not_56_out, b2);
  not not_57 (not_57_out, reset);
  and and_13 (and_13_out, not_29_out, not_30_out, not_31_out, b2, not_32_out, not_33_out);
  and and_14 (and_14_out, not_34_out, not_35_out, not_36_out, State_q[0], not_37_out, not_38_out, not_39_out);
  and and_15 (and_15_out, not_40_out, State_q[1], not_41_out, not_42_out);
  and and_16 (and_16_out, not_43_out, State_q[1], b1);
  and and_17 (and_17_out, not_44_out, State_q[1], b1);
  and and_18 (and_18_out, not_45_out, State_q[1], b2);
  and and_19 (and_19_out, not_46_out, State_q[1], b2);
  and and_20 (and_20_out, not_47_out, State_q[2], State_q[1], not_48_out);
  and and_21 (and_21_out, State_q[3], not_49_out, not_50_out, not_51_out, not_52_out, not_53_out, not_54_out);
  and and_22 (and_22_out, State_q[3], not_55_out, State_q[0], not_56_out, b1, not_57_out);
  not not_58 (not_58_out, State_q[3]);
  not not_59 (not_59_out, b2);
  not not_60 (not_60_out, b1);
  not not_61 (not_61_out, reset);
  not not_62 (not_62_out, State_q[2]);
  not not_63 (not_63_out, State_q[1]);
  not not_64 (not_64_out, State_q[0]);
  not not_65 (not_65_out, b2);
  not not_66 (not_66_out, b1);
  not not_67 (not_67_out, reset);
  or or_6 (or_9_out[1], and_13_out, and_14_out, and_15_out, and_16_out, and_17_out, and_18_out, and_19_out, and_20_out, and_21_out, and_22_out);
  not not_68 (not_68_out, State_q[3]);
  not not_69 (not_69_out, State_q[0]);
  not not_70 (not_70_out, b2);
  not not_71 (not_71_out, reset);
  not not_72 (not_72_out, State_q[3]);
  not not_73 (not_73_out, State_q[1]);
  not not_74 (not_74_out, State_q[3]);
  not not_75 (not_75_out, State_q[3]);
  not not_76 (not_76_out, State_q[3]);
  not not_77 (not_77_out, State_q[1]);
  not not_78 (not_78_out, reset);
  not not_79 (not_79_out, State_q[3]);
  and and_23 (and_23_out, not_58_out, State_q[1], State_q[0], not_59_out, not_60_out, not_61_out);
  and and_24 (and_24_out, not_68_out, State_q[2], not_69_out, not_70_out, not_71_out);
  and and_25 (and_25_out, not_72_out, State_q[2], not_73_out, b1);
  and and_26 (and_26_out, not_74_out, State_q[2], b1, reset);
  and and_27 (and_27_out, not_75_out, State_q[2], b2, reset);
  and and_28 (and_28_out, not_76_out, State_q[2], not_77_out, State_q[0], not_78_out);
  and and_29 (and_29_out, not_79_out, State_q[2], State_q[1], b2);
  and and_30 (and_30_out, State_q[3], not_62_out, not_63_out, not_64_out, not_65_out, not_66_out, not_67_out);
  not not_80 (not_80_out, State_q[2]);
  not not_81 (not_81_out, State_q[0]);
  not not_82 (not_82_out, b1);
  not not_83 (not_83_out, reset);
  not not_84 (not_84_out, State_q[3]);
  not not_85 (not_85_out, b2);
  not not_86 (not_86_out, reset);
  not not_87 (not_87_out, State_q[2]);
  not not_88 (not_88_out, State_q[2]);
  not not_89 (not_89_out, State_q[2]);
  not not_90 (not_90_out, State_q[1]);
  not not_91 (not_91_out, reset);
  not not_92 (not_92_out, State_q[2]);
  not not_93 (not_93_out, State_q[0]);
  not not_94 (not_94_out, reset);
  or or_7 (or_9_out[2], and_23_out, and_24_out, and_25_out, and_26_out, and_27_out, and_28_out, and_29_out, and_30_out);
  and and_31 (and_31_out, not_80_out, not_81_out, b2, not_82_out, not_83_out);
  and and_32 (and_32_out, not_84_out, State_q[2], State_q[1], State_q[0], not_85_out, b1, not_86_out);
  and and_33 (and_33_out, State_q[3], not_87_out, b1);
  and and_34 (and_34_out, State_q[3], not_88_out, b2);
  and and_35 (and_35_out, State_q[3], not_89_out, not_90_out, State_q[0], not_91_out);
  and and_36 (and_36_out, State_q[3], not_92_out, State_q[1], not_93_out, not_94_out);
  or or_8 (or_9_out[3], and_31_out, and_32_out, and_33_out, and_34_out, and_35_out, and_36_out);
  not not_95 (not_95_out, State_q[3]);
  not not_96 (not_96_out, State_q[2]);
  not not_97 (not_97_out, b1);
  not not_98 (not_98_out, reset);
  not not_99 (not_99_out, State_q[3]);
  not not_100 (not_100_out, State_q[1]);
  not not_101 (not_101_out, b1);
  not not_102 (not_102_out, reset);
  not not_103 (not_103_out, State_q[3]);
  not not_104 (not_104_out, b2);
  not not_105 (not_105_out, b1);
  not not_106 (not_106_out, reset);
  not not_107 (not_107_out, State_q[2]);
  not not_108 (not_108_out, State_q[1]);
  not not_109 (not_109_out, b2);
  not not_110 (not_110_out, b1);
  not not_111 (not_111_out, reset);
  not not_112 (not_112_out, State_q[2]);
  not not_113 (not_113_out, State_q[0]);
  not not_114 (not_114_out, b2);
  not not_115 (not_115_out, b1);
  not not_116 (not_116_out, reset);
  not not_117 (not_117_out, State_q[3]);
  not not_118 (not_118_out, State_q[2]);
  not not_119 (not_119_out, b2);
  not not_120 (not_120_out, reset);
  not not_121 (not_121_out, State_q[3]);
  not not_122 (not_122_out, State_q[1]);
  not not_123 (not_123_out, b2);
  not not_124 (not_124_out, reset);
  not not_125 (not_125_out, State_q[2]);
  not not_126 (not_126_out, State_q[3]);
  not not_127 (not_127_out, State_q[3]);
  not not_128 (not_128_out, State_q[1]);
  not not_129 (not_129_out, State_q[3]);
  not not_130 (not_130_out, State_q[2]);
  not not_131 (not_131_out, State_q[3]);
  not not_132 (not_132_out, State_q[2]);
  and and_37 (and_37_out, not_117_out, not_118_out, not_119_out, b1, not_120_out);
  and and_38 (and_38_out, not_121_out, not_122_out, not_123_out, b1, not_124_out);
  and and_39 (and_39_out, not_125_out, State_q[0], b1);
  and and_40 (and_40_out, not_126_out, State_q[0], b1, reset);
  and and_41 (and_41_out, not_127_out, not_128_out, State_q[0], b2);
  and and_42 (and_42_out, not_129_out, State_q[0], b2, reset);
  and and_43 (and_43_out, not_130_out, State_q[0], b2, reset);
  and and_44 (and_44_out, not_131_out, State_q[0], b2, b1);
  and and_45 (and_45_out, not_95_out, not_96_out, State_q[1], b2, not_97_out, not_98_out);
  and and_46 (and_46_out, not_132_out, State_q[1], State_q[0], b2);
  and and_47 (and_47_out, not_99_out, State_q[2], not_100_out, b2, not_101_out, not_102_out);
  and and_48 (and_48_out, not_103_out, State_q[2], State_q[0], not_104_out, not_105_out, not_106_out);
  and and_49 (and_49_out, State_q[3], not_107_out, not_108_out, not_109_out, not_110_out, not_111_out);
  and and_50 (and_50_out, State_q[3], not_112_out, not_113_out, not_114_out, not_115_out, not_116_out);
  or or_9 (or_9_out[0], and_37_out, and_38_out, and_39_out, and_40_out, and_41_out, and_42_out, and_43_out, and_44_out, and_45_out, and_46_out, and_47_out, and_48_out, and_49_out, and_50_out);

  assign b1_win = a;
  assign g = b2_win;

  // Notes on the sheet:
  //   s3
  //   s2
  //   s1
  //   s0
  //   n3
  //   n2
  //   n1
  //   n0
  //   B2
  //   Reset
endmodule

module game (
);

  wire button_1_out, button_2_out, button_3_out, button_4_out, clock_1_out, control_unit_1_a,
       control_unit_1_b, control_unit_1_b1_win, control_unit_1_b2_win, control_unit_1_c, control_unit_1_d,
       control_unit_1_e, control_unit_1_f, control_unit_1_g;
  wire [3:0] score_1_b1_1, score_1_b1_2, score_1_b1_3, score_1_b2_1, score_1_b2_2, score_1_b2_3;

  Hex_Digit_Display hex_digit_display_1 (.value(score_1_b1_3));  // open: dp
  Button button_1 (.out(button_1_out));
  Hex_Digit_Display hex_digit_display_2 (.value(score_1_b1_1));  // open: dp
  Hex_Digit_Display hex_digit_display_3 (.value(score_1_b1_2));  // open: dp
  Clock clock_1 (.out(clock_1_out));
  LED led_1 (.in(control_unit_1_a));
  LED led_2 (.in(control_unit_1_b));
  Control_Unit control_unit_1 (
    .b1(button_1_out), .reset(button_2_out), .b2(button_3_out), .clk(clock_1_out), .a(control_unit_1_a),
    .b(control_unit_1_b), .c(control_unit_1_c), .d(control_unit_1_d), .e(control_unit_1_e),
    .f(control_unit_1_f), .g(control_unit_1_g), .b1_win(control_unit_1_b1_win), .b2_win(control_unit_1_b2_win));
  LED led_3 (.in(control_unit_1_e));
  LED led_4 (.in(control_unit_1_c));
  LED led_5 (.in(control_unit_1_d));
  Button button_2 (.out(button_2_out));
  LED led_6 (.in(control_unit_1_g));
  LED led_7 (.in(control_unit_1_f));
  Button button_3 (.out(button_3_out));
  score score_1 (
    .b1_win(control_unit_1_b1_win), .reset_score(button_4_out), .b2_win(control_unit_1_b2_win),
    .b1_2(score_1_b1_2), .b1_3(score_1_b1_3), .b2_2(score_1_b2_2), .b2_3(score_1_b2_3), .b1_1(score_1_b1_1),
    .b2_1(score_1_b2_1));
  Hex_Digit_Display hex_digit_display_4 (.value(score_1_b2_3));  // open: dp
  Hex_Digit_Display hex_digit_display_5 (.value(score_1_b2_2));  // open: dp
  Button button_4 (.out(button_4_out));
  Hex_Digit_Display hex_digit_display_6 (.value(score_1_b2_1));  // open: dp

  // Notes on the sheet:
  //   B1
  //   B1 Score
  //   b
  //   c
  //   a
  //   Reset
  //   d
  //   e
  //   Control Unit
  //   g
  //   f
  //   Score Unit
  //   B2
  //   B2 Score
  //   reset score
endmodule

module score (
  input  b1_win,
  input  reset_score,
  input  b2_win,
  output [3:0] b1_2,
  output [3:0] b1_3,
  output [3:0] b2_2,
  output [3:0] b2_3,
  output [3:0] b1_1,
  output [3:0] b2_1
);

  wire counter_2_carry, counter_3_carry, counter_5_carry, counter_6_carry, or_1_out, or_2_out, or_3_out,
       or_4_out;

  Counter #(.width(4), .max('h9)) counter_1 (
    .Q(b1_3), .clk(counter_2_carry), .clr(reset_score));  // open: load, D, count, carry
  Counter #(.width(4), .max('ha)) counter_2 (
    .Q(b1_2), .carry(counter_2_carry), .clk(counter_3_carry), .clr(or_2_out));  // open: load, D, count
  Counter #(.width(4), .max('ha)) counter_3 (
    .Q(b1_1), .carry(counter_3_carry), .clk(b1_win), .clr(or_1_out));  // open: load, D, count
  or or_1 (or_1_out, counter_3_carry, reset_score);
  or or_2 (or_2_out, counter_2_carry, reset_score);
  Counter #(.width(4), .max('h9)) counter_4 (
    .Q(b2_3), .clk(counter_5_carry), .clr(reset_score));  // open: load, D, count, carry
  Counter #(.width(4), .max('ha)) counter_5 (
    .Q(b2_2), .carry(counter_5_carry), .clk(counter_6_carry), .clr(or_4_out));  // open: load, D, count
  Counter #(.width(4), .max('ha)) counter_6 (
    .Q(b2_1), .carry(counter_6_carry), .clk(b2_win), .clr(or_3_out));  // open: load, D, count
  or or_3 (or_3_out, reset_score, counter_6_carry);
  or or_4 (or_4_out, reset_score, counter_5_carry);
endmodule
