// Logisim project 171044098.circ as structural Verilog: 4 circuits, main circuit Multiplier
module Multiplier (
  input  [15:0] a,
  input  [15:0] b,
  output [15:0] Result
);

  wire Calculate_out, clock_1_out, Control_Unit_la, Control_Unit_lb, Control_Unit_lm, Control_Unit_lres,
       Control_Unit_sa, Control_Unit_smult, Control_Unit_sop, Datapath_bigger, Datapath_equal, Datapath_less;

  Button Calculate (.out(Calculate_out));
  Clock clock_1 (.out(clock_1_out));
  Control_Unit Control_Unit (
    .C(Calculate_out), .clk(clock_1_out), .La(Control_Unit_la), .Lb(Control_Unit_lb), .Lm(Control_Unit_lm),
    .Lres(Control_Unit_lres), .Sa(Control_Unit_sa), .Sop(Control_Unit_sop), .Smult(Control_Unit_smult),
    .L(Datapath_less), .E(Datapath_equal), .B(Datapath_bigger));
  // Probe on a
  // Probe on b
  DataPath Datapath (
    .La(Control_Unit_la), .a(a), .b(b), .Sa(Control_Unit_sa), .Lb(Control_Unit_lb), .clk(clock_1_out),
    .Sopr(Control_Unit_sop), .Lmult(Control_Unit_lm), .Smult(Control_Unit_smult), .Lres(Control_Unit_lres),
    .result(Result), .bigger(Datapath_bigger), .equal(Datapath_equal), .less(Datapath_less));
  // Probe on Result

  // Notes on the sheet:
  //   *Enable Clock
  //   *Enter a and b numbers
  //   *Click Calculate Button
  //   *Change Numbers Click Again
  //   *Result can be between -32.768 and 32.767
endmodule

module check (
  input  [15:0] a_in,
  input  [15:0] b_in,
  output [15:0] a_out,
  output [15:0] b_out
);

  wire comparator_1_lt;
  wire [15:0] negator_1_out, negator_2_out;

  Comparator #(.width(16)) comparator_1 (.a(a_in), .b({16{1'b0}}), .lt(comparator_1_lt));  // open: gt, eq
  Negator #(.width(16)) negator_1 (.in(a_in), .out(negator_1_out));
  Negator #(.width(16)) negator_2 (.in(b_in), .out(negator_2_out));
  Multiplexer #(.width(16), .enable("false")) multiplexer_1 (
    .in0(a_in), .in1(negator_1_out), .out(a_out), .sel(comparator_1_lt));
  Multiplexer #(.width(16), .enable("false")) multiplexer_2 (
    .in0(b_in), .in1(negator_2_out), .out(b_out), .sel(comparator_1_lt));

  // Notes on the sheet:
  //   0
  //   a < 0 
  //   This module cheks a input and it is reproduced them if it is neccesary.
  //   (To perform negative number multiplications)
  //   a
  //   -a
  //   b
  //   -b
  //   }
  //   if (a < 0) { 	
  //   a = -1*a ;
  //   b = -1*b ;
endmodule

module DataPath (
  input  La,
  input  [15:0] a,
  input  [15:0] b,
  input  Sa,
  input  Lb,
  input  clk,
  input  Sopr,
  input  Lmult,
  input  Smult,
  input  Lres,
  output [15:0] result,
  output bigger,
  output equal,
  output less
);

  wire [15:0] a_q, adder_1_out, b_q, Check_a_a_out, Check_a_b_out, demultiplexer_1_out0,
       demultiplexer_1_out1, mult_q, multiplexer_1_out, multiplexer_2_out, multiplexer_3_out,
       multiplexer_4_out, negator_1_out;

  check Check_a (.a_out(Check_a_a_out), .b_out(Check_a_b_out), .a_in(a), .b_in(b));
  Comparator #(.width(16)) comparator_1 (.a(a_q), .b({16{1'b0}}), .gt(bigger), .eq(equal), .lt(less));
  Multiplexer #(.width(16), .enable("false")) multiplexer_1 (
    .in0(Check_a_a_out), .in1(demultiplexer_1_out0), .out(multiplexer_1_out), .sel(Sa));
  Multiplexer #(.width(16), .enable("false")) multiplexer_2 (
    .in0({16{1'b0}}), .in1(demultiplexer_1_out1), .out(multiplexer_2_out), .sel(Smult));
  Register #(.width(16)) u_a (.D(multiplexer_1_out), .en(La), .Q(a_q), .clk(clk));  // open: clr
  Register #(.width(16)) u_b (.D(Check_a_b_out), .en(Lb), .Q(b_q), .clk(clk));  // open: clr
  Negator #(.width(16)) negator_1 (.in(16'h1), .out(negator_1_out));
  Register #(.width(16)) mult (.D(multiplexer_2_out), .en(Lmult), .Q(mult_q), .clk(clk));  // open: clr
  Multiplexer #(.width(16), .enable("false")) multiplexer_3 (.in0(a_q), .in1(b_q), .out(multiplexer_3_out), .sel(Sopr));
  Multiplexer #(.width(16), .enable("false")) multiplexer_4 (
    .in0(negator_1_out), .in1(mult_q), .out(multiplexer_4_out), .sel(Sopr));
  Register #(.width(16)) res (.D(mult_q), .en(Lres), .Q(result), .clk(clk));  // open: clr
  Adder #(.width(16)) adder_1 (.a(multiplexer_3_out), .b(multiplexer_4_out), .out(adder_1_out));  // open: cin, cout
  Demultiplexer #(.width(16), .enable("false")) demultiplexer_1 (
    .out0(demultiplexer_1_out0), .out1(demultiplexer_1_out1), .in(adder_1_out), .sel(Sopr));

  // Notes on the sheet:
  //   Datapath Module of Project (Check Report for more information)
  //   Mux a
  //   Mux mult
  //   a
  //   b
  //   mult
  //   Mux varible1
  //   Mux varible2
  //   -1
  //   One Adder
  //   Mux result
endmodule

module Control_Unit (
  input  C,
  input  L,
  input  E,
  input  B,
  input  clk,
  output La,
  output Lb,
  output Lm,
  output Lres,
  output Sa,
  output Sop,
  output Smult
);

  wire and_1_out, and_2_out, and_8_out, and_9_out, and_10_out, and_11_out, and_12_out, and_13_out,
       and_14_out, and_15_out, and_16_out, and_17_out, not_1_out, not_2_out, not_3_out, not_4_out, not_5_out,
       not_6_out, not_7_out, not_8_out, not_9_out, not_10_out, not_11_out, not_12_out, not_13_out,
       not_14_out, not_15_out, not_16_out, not_17_out, not_18_out, not_19_out, not_20_out, not_21_out,
       not_22_out, not_23_out, not_24_out, not_25_out, not_26_out, not_27_out, not_28_out, not_29_out,
       not_30_out, not_31_out, not_32_out, not_33_out, not_34_out, not_35_out, not_36_out, not_37_out,
       not_38_out, not_39_out, not_40_out;
  wire [2:0] or_4_out, State_q;

  not not_1 (not_1_out, State_q[2]);
  not not_2 (not_2_out, State_q[1]);
  not not_3 (not_3_out, State_q[1]);
  not not_4 (not_4_out, State_q[0]);
  not not_5 (not_5_out, State_q[2]);
  not not_6 (not_6_out, State_q[1]);
  not not_7 (not_7_out, State_q[1]);
  not not_8 (not_8_out, State_q[0]);
  not not_9 (not_9_out, State_q[2]);
  not not_10 (not_10_out, State_q[2]);
  Register #(.width(3)) State (.D(or_4_out), .en(1'b1), .Q(State_q), .clk(clk));  // open: clr
  and and_1 (and_1_out, not_1_out, not_2_out, State_q[0]);
  and and_2 (and_2_out, State_q[2], not_3_out, not_4_out);
  and and_3 (Lb, not_5_out, State_q[0]);
  and and_4 (Lres, State_q[2], not_6_out, State_q[0]);
  and and_5 (Sa, State_q[2], not_7_out, not_8_out);
  and and_6 (Sop, not_9_out, State_q[1], State_q[0]);
  and and_7 (Smult, not_10_out, State_q[1], State_q[0]);
  not not_11 (not_11_out, State_q[2]);
  not not_12 (not_12_out, L);
  not not_13 (not_13_out, B);
  not not_14 (not_14_out, State_q[2]);
  not not_15 (not_15_out, E);
  not not_16 (not_16_out, B);
  not not_17 (not_17_out, State_q[2]);
  or or_1 (La, and_1_out, and_2_out);
  and and_8 (and_8_out, not_11_out, State_q[1], not_12_out, E, not_13_out);
  and and_9 (and_9_out, not_14_out, State_q[1], L, not_15_out, not_16_out);
  and and_10 (and_10_out, not_17_out, State_q[1], State_q[0]);
  or or_2 (or_4_out[2], and_8_out, and_9_out, and_10_out);
  not not_18 (not_18_out, State_q[2]);
  not not_19 (not_19_out, State_q[1]);
  not not_20 (not_20_out, State_q[2]);
  not not_21 (not_21_out, State_q[0]);
  not not_22 (not_22_out, L);
  not not_23 (not_23_out, E);
  not not_24 (not_24_out, State_q[1]);
  not not_25 (not_25_out, State_q[0]);
  and and_11 (and_11_out, not_18_out, not_19_out, State_q[0]);
  and and_12 (and_12_out, not_20_out, State_q[1], not_21_out, not_22_out, not_23_out, B);
  and and_13 (and_13_out, State_q[2], not_24_out, not_25_out);
  or or_3 (or_4_out[1], and_11_out, and_12_out, and_13_out);
  not not_26 (not_26_out, State_q[2]);
  not not_27 (not_27_out, State_q[1]);
  not not_28 (not_28_out, State_q[0]);
  not not_29 (not_29_out, State_q[2]);
  not not_30 (not_30_out, State_q[0]);
  not not_31 (not_31_out, L);
  not not_32 (not_32_out, E);
  not not_33 (not_33_out, State_q[2]);
  not not_34 (not_34_out, State_q[0]);
  not not_35 (not_35_out, L);
  not not_36 (not_36_out, B);
  not not_37 (not_37_out, State_q[2]);
  not not_38 (not_38_out, State_q[0]);
  not not_39 (not_39_out, E);
  not not_40 (not_40_out, B);
  and and_14 (and_14_out, not_26_out, not_27_out, not_28_out, C);
  and and_15 (and_15_out, not_29_out, State_q[1], not_30_out, not_31_out, not_32_out, B);
  and and_16 (and_16_out, not_33_out, State_q[1], not_34_out, not_35_out, E, not_36_out);
  and and_17 (and_17_out, not_37_out, State_q[1], not_38_out, L, not_39_out, not_40_out);
  or or_4 (or_4_out[0], and_14_out, and_15_out, and_16_out, and_17_out);

  assign Lm = Lb;

  // Notes on the sheet:
  //   s2
  //   s1
  //   s0
  //   Control Unit Module of Project(Check Report for more information)
  //   n2
  //   n1
  //   n0
endmodule
